// Digital circuit au4.dig as structural Verilog
module au4 (
  input  [3:0] A,
  input  [3:0] B,
  input  sub,
  output [3:0] S,
  output V
);

  wire adder_2_v, adder_3_v, adder_4_v, xor_1_out, xor_2_out, xor_3_out, xor_4_out;

  xor xor_1 (xor_1_out, B[3], sub);
  adder adder_1 (.A(A[3]), .B(xor_1_out), .C(adder_2_v), .S(S[3]), .V(V));
  xor xor_2 (xor_2_out, B[2], sub);
  adder adder_2 (.A(A[2]), .B(xor_2_out), .C(adder_3_v), .S(S[2]), .V(adder_2_v));
  xor xor_3 (xor_3_out, B[1], sub);
  adder adder_3 (.A(A[1]), .B(xor_3_out), .C(adder_4_v), .S(S[1]), .V(adder_3_v));
  xor xor_4 (xor_4_out, B[0], sub);
  adder adder_4 (.A(A[0]), .B(xor_4_out), .C(sub), .S(S[0]), .V(adder_4_v));
endmodule
