// Digital circuit basic.dig as structural Verilog
module basic (
  input  X,
  input  Y,
  output [3:0] \not ,
  output [3:0] \or ,
  output [3:0] \and ,
  output [3:0] \nor ,
  output [3:0] \nand ,
  output [3:0] \xor ,
  output [3:0] eqv
);

  wire and_2_out, and_3_out, and_4_out, nand_3_out, nand_4_out, nand_5_out, nand_6_out, nand_7_out,
       nand_11_out, nand_12_out, nor_3_out, nor_4_out, nor_5_out, nor_6_out, nor_7_out, nor_11_out,
       nor_12_out, not_2_out, not_3_out, or_2_out;

  not not_1 (\not [1], X);
  or or_1 (\or [1], X, Y);
  and and_1 (\and [1], X, Y);
  nor nor_1 (\nor [0], X, Y);
  nand nand_1 (\nand [0], X, Y);
  xor xor_1 (\xor [0], X, Y);
  xnor xnor_1 (eqv[0], X, Y);
  not not_2 (not_2_out, X);
  not not_3 (not_3_out, Y);
  or or_2 (or_2_out, X, Y);
  and and_2 (and_2_out, X, Y);
  and and_3 (and_3_out, not_2_out, Y);
  and and_4 (and_4_out, X, not_3_out);
  not not_4 (\nor [3], or_2_out);
  not not_5 (\nand [2], and_2_out);
  or or_3 (\xor [1], and_3_out, and_4_out);
  not not_6 (eqv[1], \xor [1]);
  nand nand_2 (\not [2], X, X);
  nand nand_3 (nand_3_out, X, X);
  nand nand_4 (nand_4_out, Y, Y);
  nand nand_5 (nand_5_out, X, Y);
  nand nand_6 (nand_6_out, X, X);
  nand nand_7 (nand_7_out, Y, Y);
  nand nand_8 (\or [2], nand_3_out, nand_4_out);
  nand nand_9 (\and [2], nand_5_out, nand_5_out);
  nand nand_10 (\nor [2], \or [2], \or [2]);
  nand nand_11 (nand_11_out, nand_6_out, Y);
  nand nand_12 (nand_12_out, X, nand_7_out);
  nand nand_13 (\xor [2], nand_11_out, nand_12_out);
  nand nand_14 (eqv[2], \xor [2], \xor [2]);
  nor nor_2 (\not [3], X, X);
  nor nor_3 (nor_3_out, X, Y);
  nor nor_4 (nor_4_out, X, X);
  nor nor_5 (nor_5_out, Y, Y);
  nor nor_6 (nor_6_out, X, X);
  nor nor_7 (nor_7_out, Y, Y);
  nor nor_8 (\or [3], nor_3_out, nor_3_out);
  nor nor_9 (\and [3], nor_4_out, nor_5_out);
  nor nor_10 (\nand [3], \and [3], \and [3]);
  nor nor_11 (nor_11_out, nor_6_out, Y);
  nor nor_12 (nor_12_out, X, nor_7_out);
  nor nor_13 (eqv[3], nor_11_out, nor_12_out);
  nor nor_14 (\xor [3], eqv[3], eqv[3]);

  assign \and [0] = \and [1];
  assign \nand [1] = \nand [2];
  assign \nor [1] = \nor [3];
  assign \not [0] = \not [1];
  assign \or [0] = \or [1];

  // Other names for the same wires on the sheet: a1 = \and [1]; a3 = \and [2]; a4 = \and [3]; n1 = \not [1];
  //   n3 = \not [2]; n4 = \not [3]; na1 = \nand [0]; na2 = \nand [2]; na4 = \nand [3]; no1 = \nor [0]; no2 = \nor [3];
  //   no3 = \nor [2]; o1 = \or [1]; o3 = \or [2]; o4 = \or [3]; x1 = \xor [0]; x2 = \xor [1]; x3 = \xor [2];
  //   x4 = \xor [3]; xn1 = eqv[0]; xn2 = eqv[1]; xn3 = eqv[2]; xn4 = eqv[3]
endmodule
