// Digital circuit mult4x4.dig as structural Verilog
module mult4x4 (
  input  [3:0] A,
  input  [3:0] B,
  output [7:0] M
);

  wire adder_2_s, adder_2_v, adder_3_v, adder_4_s, adder_4_v, adder_5_s, adder_5_v, adder_6_v, adder_7_s,
       adder_7_v, adder_8_s, adder_8_v, adder_9_v, adder_10_s, adder_10_v, adder_11_v, adder_12_v, and_1_out,
       and_2_out, and_3_out, and_4_out, and_5_out, and_6_out, and_7_out, and_8_out, and_9_out, and_10_out,
       and_11_out, and_12_out, and_13_out, and_14_out, and_15_out;

  and and_1 (and_1_out, A[3], B[3]);
  adder adder_1 (.A(and_1_out), .B(adder_2_v), .C(adder_3_v), .S(M[6]), .V(M[7]));
  and and_2 (and_2_out, A[3], B[2]);
  adder adder_2 (.A(and_2_out), .B(adder_4_v), .C(adder_5_v), .S(adder_2_s), .V(adder_2_v));
  and and_3 (and_3_out, A[2], B[3]);
  adder adder_3 (.A(and_3_out), .B(adder_2_s), .C(adder_6_v), .S(M[5]), .V(adder_3_v));
  and and_4 (and_4_out, A[3], B[1]);
  adder adder_4 (.A(and_4_out), .B(1'b0), .C(adder_7_v), .S(adder_4_s), .V(adder_4_v));
  and and_5 (and_5_out, A[2], B[2]);
  adder adder_5 (.A(and_5_out), .B(adder_4_s), .C(adder_8_v), .S(adder_5_s), .V(adder_5_v));
  and and_6 (and_6_out, A[1], B[3]);
  adder adder_6 (.A(and_6_out), .B(adder_5_s), .C(adder_9_v), .S(M[4]), .V(adder_6_v));
  and and_7 (and_7_out, A[3], B[0]);
  and and_8 (and_8_out, A[2], B[1]);
  adder adder_7 (.A(and_8_out), .B(and_7_out), .C(adder_10_v), .S(adder_7_s), .V(adder_7_v));
  and and_9 (and_9_out, A[1], B[2]);
  adder adder_8 (.A(and_9_out), .B(adder_7_s), .C(adder_11_v), .S(adder_8_s), .V(adder_8_v));
  and and_10 (and_10_out, A[0], B[3]);
  adder adder_9 (.A(and_10_out), .B(adder_8_s), .C(1'b0), .S(M[3]), .V(adder_9_v));
  and and_11 (and_11_out, A[2], B[0]);
  and and_12 (and_12_out, A[1], B[1]);
  adder adder_10 (.A(and_12_out), .B(and_11_out), .C(adder_12_v), .S(adder_10_s), .V(adder_10_v));
  and and_13 (and_13_out, A[0], B[2]);
  adder adder_11 (.A(and_13_out), .B(adder_10_s), .C(1'b0), .S(M[2]), .V(adder_11_v));
  and and_14 (and_14_out, A[1], B[0]);
  and and_15 (and_15_out, A[0], B[1]);
  adder adder_12 (.A(and_15_out), .B(and_14_out), .C(1'b0), .S(M[1]), .V(adder_12_v));
  and and_16 (M[0], A[0], B[0]);
endmodule
