// Digital circuit mux2.dig as structural Verilog
module mux2 (
  input  A,
  input  B,
  input  sel,
  output Z
);

  wire and_1_out, and_2_out;

  and and_1 (and_1_out, A, ~sel);  // And
  and and_2 (and_2_out, B, sel);
  or or_1 (Z, and_1_out, and_2_out);
endmodule
