// Digital circuit mux8.dig as structural Verilog
module mux8 (
  input  A,
  input  B,
  input  C,
  input  D,
  input  E,
  input  F,
  input  G,
  input  H,
  input  [2:0] sel,
  output Z
);

  wire and_1_out, and_2_out, and_3_out, and_4_out, and_5_out, and_6_out, and_7_out, and_8_out;

  and and_1 (and_1_out, A, ~sel[2], ~sel[1], ~sel[0]);  // And
  and and_2 (and_2_out, C, ~sel[2], sel[1], ~sel[0]);  // And
  and and_3 (and_3_out, E, sel[2], ~sel[1], ~sel[0]);  // And
  and and_4 (and_4_out, G, sel[2], sel[1], ~sel[0]);  // And
  and and_5 (and_5_out, B, ~sel[2], ~sel[1], sel[0]);  // And
  and and_6 (and_6_out, D, ~sel[2], sel[1], sel[0]);  // And
  and and_7 (and_7_out, F, sel[2], ~sel[1], sel[0]);  // And
  and and_8 (and_8_out, H, sel[2], sel[1], sel[0]);
  or or_1 (Z, and_1_out, and_5_out, and_2_out, and_6_out, and_3_out, and_7_out, and_4_out, and_8_out);
endmodule
