// Digital circuit rom4x6.dig as structural Verilog
module rom4x6 (
  input  [1:0] \end ,
  input  leia,
  output [5:0] dado
);

  wire and_1_out, and_2_out, and_3_out, and_4_out, nfet_1_d, nfet_5_d, nfet_7_d, nfet_8_d, nfet_11_d,
       pullup_4_out;

  and and_1 (and_1_out, leia, ~\end [1], ~\end [0]);  // And
  and and_2 (and_2_out, leia, ~\end [1], \end [0]);  // And
  and and_3 (and_3_out, leia, \end [1], ~\end [0]);  // And
  and and_4 (and_4_out, leia, \end [1], \end [0]);
  NFET nfet_1 (.G(and_1_out), .D(nfet_1_d), .S(1'b0));
  NFET nfet_2 (.G(and_2_out), .D(nfet_1_d), .S(1'b0));
  NFET nfet_3 (.G(and_3_out), .D(nfet_1_d), .S(1'b0));
  NFET nfet_4 (.G(and_4_out), .D(nfet_1_d), .S(1'b0));
  PullUp pullup_1 (.out(nfet_1_d));
  NFET nfet_5 (.G(and_1_out), .D(nfet_5_d), .S(1'b0));
  NFET nfet_6 (.G(and_3_out), .D(nfet_5_d), .S(1'b0));
  PullUp pullup_2 (.out(nfet_5_d));
  NFET nfet_7 (.G(and_2_out), .D(nfet_7_d), .S(1'b0));
  PullUp pullup_3 (.out(nfet_7_d));
  PullUp pullup_4 (.out(pullup_4_out));
  NFET nfet_8 (.G(and_1_out), .D(nfet_8_d), .S(1'b0));
  NFET nfet_9 (.G(and_3_out), .D(nfet_8_d), .S(1'b0));
  NFET nfet_10 (.G(and_4_out), .D(nfet_8_d), .S(1'b0));
  PullUp pullup_5 (.out(nfet_8_d));
  NFET nfet_11 (.G(and_2_out), .D(nfet_11_d), .S(1'b0));
  NFET nfet_12 (.G(and_3_out), .D(nfet_11_d), .S(1'b0));
  NFET nfet_13 (.G(and_4_out), .D(nfet_11_d), .S(1'b0));
  PullUp pullup_6 (.out(nfet_11_d));
  not not_1 (dado[0], nfet_11_d);
  not not_2 (dado[1], nfet_8_d);
  not not_3 (dado[2], pullup_4_out);
  not not_4 (dado[3], nfet_7_d);
  not not_5 (dado[4], nfet_5_d);
  not not_6 (dado[5], nfet_1_d);
endmodule
