// Digital circuit switch.dig as structural Verilog
module switch (
  input  in_1,
  input  in_2
);

  wire nfet_1_s, relay_1_p4, switch_1_b, switch_2_b;

  Switch switch_1 (.A(1'b1), .B(switch_1_b));
  // Relay relay_1: pin names not known; wires that end beside it: in_1, 1'b1, 1'b0, relay_1_p4
  Switch switch_2 (.A(switch_1_b), .B(switch_2_b));
  Switch switch_3 (.A(switch_1_b), .B(switch_2_b));
  NFET nfet_1 (.G(in_2), .D(1'b1), .S(nfet_1_s));
  LED led_1 (.in(switch_2_b));
  LED led_2 (.in(relay_1_p4));
  LED led_3 (.in(nfet_1_s));
endmodule
