// Digital circuit switchlogic.dig as structural Verilog
module switchlogic (
  input  X,
  input  Y,
  input  Z,
  output A,
  output B,
  output C,
  output D
);

  wire relay_4_p5, relay_5_p1;

  // Relay relay_1: pin names not known; wires that end beside it: X, 1'b1, Y, 1'b0, B, 1'b0
  // Relay relay_2: pin names not known; wires that end beside it: 1'b1, Z, B, 1'b0
  // Relay relay_3: pin names not known; wires that end beside it: 1'b1, B
  or or_1 (A, X, Y, Z);
  PullDown pulldown_1 (.out(B));
  // Relay relay_4: pin names not known; wires that end beside it: X, 1'b1, Y, 1'b0, relay_4_p5, 1'b0
  // Relay relay_5: pin names not known; wires that end beside it: relay_5_p1, Z, relay_4_p5, 1'b0
  // Relay relay_6: pin names not known; wires that end beside it: relay_5_p1, D
  and and_1 (C, X, Y, Z);
  PullDown pulldown_2 (.out(D));
endmodule
