// Digital circuit twoinput.dig as structural Verilog
module twoinput (
  input  X,
  input  Y,
  output A,
  output B,
  output C,
  output D,
  output E,
  output F,
  output G,
  output H,
  output I,
  output J,
  output K,
  output L,
  output M,
  output N,
  output O,
  output P
);

  wire not_1_out, not_3_out, not_5_out, not_6_out;

  not not_1 (not_1_out, Y);
  nor nor_1 (B, X, Y);
  nor nor_2 (C, X, not_1_out);
  not not_2 (D, X);
  not not_3 (not_3_out, X);
  nor nor_3 (E, not_3_out, Y);
  xor xor_1 (G, X, Y);
  nand nand_1 (H, X, Y);
  not not_4 (F, Y);
  not not_5 (not_5_out, X);
  and and_1 (I, X, Y);
  xnor xnor_1 (J, X, Y);
  or or_1 (L, not_5_out, Y);
  not not_6 (not_6_out, Y);
  or or_2 (N, X, not_6_out);
  or or_3 (O, X, Y);

  assign A = 1'b0;
  assign K = Y;
  assign M = X;
  assign P = 1'b1;
endmodule
