// Digital circuit votacao.dig as structural Verilog
module votacao (
  input  A,
  input  B,
  input  C,
  output Y
);

  wire and_1_out, and_2_out, and_3_out;

  and and_1 (and_1_out, A, C);
  and and_2 (and_2_out, A, B);
  and and_3 (and_3_out, B, C);
  or or_1 (Y, and_1_out, and_2_out, and_3_out);
endmodule
