// Digital circuit fpga2x2.dig as structural Verilog
module fpga2x2 (
  input  dcfg,
  input  rcfg,
  input  relogio,
  input  e0,
  input  e1,
  input  e2,
  input  e3,
  input  e4,
  input  e5,
  input  e6,
  input  e7,
  input  e8,
  input  e9,
  input  e10,
  input  e11,
  input  e12,
  input  e13,
  input  e14,
  input  e15,
  output s0,
  output s1,
  output s2,
  output s3,
  output s4,
  output s5,
  output s6,
  output s7,
  output s8,
  output s9,
  output s10,
  output s11,
  output s12,
  output s13,
  output s14,
  output s15
);

  wire lut4_1_q, lut4_1_s, lut4_1_scfg, lut4_2_q, lut4_2_s, lut4_2_scfg, lut4_3_q, lut4_3_s, lut4_3_scfg,
       lut4_4_q, lut4_4_s, lut4_4_scfg, rota4_1_scfg, rota4_1_sl0, rota4_1_sl1, rota4_1_ss0, rota4_1_ss1,
       rota4_2_scfg, rota4_2_sl0, rota4_2_sl1, rota4_2_sn0, rota4_2_sn1, rota4_3_scfg, rota4_3_so0,
       rota4_3_so1, rota4_3_ss0, rota4_3_ss1, rota4_4_sn0, rota4_4_sn1, rota4_4_so0, rota4_4_so1;

  rota4 rota4_1 (
    .el0(rota4_3_so0), .el1(rota4_3_so1), .sl0(rota4_1_sl0), .sl1(rota4_1_sl1), .scfg(rota4_1_scfg),
    .so0(s0), .so1(s1), .eo0(e0), .eo1(e1), .en0(e14), .en1(e15), .sn0(s14), .sn1(s15), .rcfg(rcfg),
    .ecfg(lut4_1_scfg), .d(lut4_1_s), .q(lut4_1_q), .ss0(rota4_1_ss0), .ss1(rota4_1_ss1), .es0(rota4_2_sn0),
    .es1(rota4_2_sn1));
  rota4 rota4_2 (
    .el0(rota4_4_so0), .el1(rota4_4_so1), .sl0(rota4_2_sl0), .sl1(rota4_2_sl1), .scfg(rota4_2_scfg),
    .so0(s2), .so1(s3), .eo0(e2), .eo1(e3), .en0(rota4_1_ss0), .en1(rota4_1_ss1), .sn0(rota4_2_sn0),
    .sn1(rota4_2_sn1), .rcfg(rcfg), .ecfg(lut4_2_scfg), .d(lut4_2_s), .q(lut4_2_q), .ss0(s4), .ss1(s5),
    .es0(e4), .es1(e5));
  lut4 lut4_1 (
    .ecfg(dcfg), .rcfg(rcfg), .e0(e14), .e1(e15), .e2(s14), .e3(s15), .c(relogio), .q(lut4_1_q),
    .s(lut4_1_s), .scfg(lut4_1_scfg));
  lut4 lut4_2 (
    .ecfg(rota4_1_scfg), .rcfg(rcfg), .e0(rota4_1_ss0), .e1(rota4_1_ss1), .e2(rota4_2_sn0), .e3(rota4_2_sn1),
    .c(relogio), .q(lut4_2_q), .s(lut4_2_s), .scfg(lut4_2_scfg));
  rota4 rota4_3 (
    .el0(e10), .el1(e11), .sl0(s10), .sl1(s11), .scfg(rota4_3_scfg), .so0(rota4_3_so0), .so1(rota4_3_so1),
    .eo0(rota4_1_sl0), .eo1(rota4_1_sl1), .en0(e12), .en1(e13), .sn0(s12), .sn1(s13), .rcfg(rcfg),
    .ecfg(lut4_3_scfg), .d(lut4_3_s), .q(lut4_3_q), .ss0(rota4_3_ss0), .ss1(rota4_3_ss1), .es0(rota4_4_sn0),
    .es1(rota4_4_sn1));
  rota4 rota4_4 (
    .el0(e8), .el1(e9), .sl0(s8), .sl1(s9), .so0(rota4_4_so0), .so1(rota4_4_so1), .eo0(rota4_2_sl0),
    .eo1(rota4_2_sl1), .en0(rota4_3_ss0), .en1(rota4_3_ss1), .sn0(rota4_4_sn0), .sn1(rota4_4_sn1),
    .rcfg(rcfg), .ecfg(lut4_4_scfg), .d(lut4_4_s), .q(lut4_4_q), .ss0(s6), .ss1(s7), .es0(e6), .es1(e7));  // open: scfg
  lut4 lut4_3 (
    .ecfg(rota4_2_scfg), .rcfg(rcfg), .e0(e12), .e1(e13), .e2(s12), .e3(s13), .c(relogio), .q(lut4_3_q),
    .s(lut4_3_s), .scfg(lut4_3_scfg));
  lut4 lut4_4 (
    .ecfg(rota4_3_scfg), .rcfg(rcfg), .e0(rota4_3_ss0), .e1(rota4_3_ss1), .e2(rota4_4_sn0), .e3(rota4_4_sn1),
    .c(relogio), .q(lut4_4_q), .s(lut4_4_s), .scfg(lut4_4_scfg));
endmodule
