// Digital circuit lut4.dig as structural Verilog
module lut4 (
  input  ecfg,
  input  rcfg,
  input  e0,
  input  e1,
  input  e2,
  input  e3,
  input  c,
  output q,
  output s,
  output scfg
);

  wire d_ff_1_q, d_ff_2_q, d_ff_3_q, d_ff_4_q, d_ff_5_q, d_ff_6_q, d_ff_7_q, d_ff_8_q, d_ff_9_q, d_ff_10_q,
       d_ff_11_q, d_ff_12_q, d_ff_13_q, d_ff_14_q, d_ff_15_q, d_ff_17_q, d_ff_18_q, multiplexer_1_out;

  D_FF d_ff_1 (.D(ecfg), .C(rcfg), .Q(d_ff_1_q));  // open: nQ
  D_FF d_ff_2 (.D(d_ff_1_q), .C(rcfg), .Q(d_ff_2_q));  // open: nQ
  D_FF d_ff_3 (.D(d_ff_2_q), .C(rcfg), .Q(d_ff_3_q));  // open: nQ
  D_FF d_ff_4 (.D(d_ff_3_q), .C(rcfg), .Q(d_ff_4_q));  // open: nQ
  D_FF d_ff_5 (.D(d_ff_4_q), .C(rcfg), .Q(d_ff_5_q));  // open: nQ
  D_FF d_ff_6 (.D(d_ff_5_q), .C(rcfg), .Q(d_ff_6_q));  // open: nQ
  D_FF d_ff_7 (.D(d_ff_6_q), .C(rcfg), .Q(d_ff_7_q));  // open: nQ
  D_FF d_ff_8 (.D(d_ff_7_q), .C(rcfg), .Q(d_ff_8_q));  // open: nQ
  D_FF d_ff_9 (.D(d_ff_8_q), .C(rcfg), .Q(d_ff_9_q));  // open: nQ
  D_FF d_ff_10 (.D(d_ff_9_q), .C(rcfg), .Q(d_ff_10_q));  // open: nQ
  D_FF d_ff_11 (.D(d_ff_10_q), .C(rcfg), .Q(d_ff_11_q));  // open: nQ
  D_FF d_ff_12 (.D(d_ff_11_q), .C(rcfg), .Q(d_ff_12_q));  // open: nQ
  D_FF d_ff_13 (.D(d_ff_12_q), .C(rcfg), .Q(d_ff_13_q));  // open: nQ
  D_FF d_ff_14 (.D(d_ff_13_q), .C(rcfg), .Q(d_ff_14_q));  // open: nQ
  D_FF d_ff_15 (.D(d_ff_14_q), .C(rcfg), .Q(d_ff_15_q));  // open: nQ
  D_FF d_ff_16 (.D(d_ff_15_q), .C(rcfg), .Q(scfg));  // open: nQ
  Multiplexer #(.Selector_Bits(4)) multiplexer_1 (
    .sel({e3, e2, e1, e0}), .in_0(d_ff_1_q), .in_1(d_ff_2_q), .in_2(d_ff_3_q), .in_3(d_ff_4_q),
    .in_4(d_ff_5_q), .in_5(d_ff_6_q), .in_6(d_ff_7_q), .in_7(d_ff_8_q), .in_8(d_ff_9_q), .in_9(d_ff_10_q),
    .in_10(d_ff_11_q), .in_11(d_ff_12_q), .in_12(d_ff_13_q), .in_13(d_ff_14_q), .in_14(d_ff_15_q),
    .in_15(scfg), .out(multiplexer_1_out));
  D_FF d_ff_17 (.D(multiplexer_1_out), .C(c), .Q(d_ff_17_q));  // open: nQ
  D_FF d_ff_18 (.D(1'b1), .C(c), .Q(d_ff_18_q));  // open: nQ
  and and_1 (s, multiplexer_1_out, d_ff_18_q);
  and and_2 (q, d_ff_17_q, d_ff_18_q);
endmodule
