// Digital circuit rota1.dig as structural Verilog
module rota1 (
  input  e0,
  input  e1,
  input  e2,
  input  e3,
  input  e4,
  input  e5,
  input  e6,
  input  e7,
  input  ecfg,
  input  rcfg,
  output s0,
  output s1,
  output scfg
);

  wire [1:0] d_ff_2_q;
  wire [2:0] d_ff_1_q;

  D_FF d_ff_1 (.D(ecfg), .C(rcfg), .Q(d_ff_1_q[0]));  // open: nQ
  D_FF d_ff_2 (.D(d_ff_1_q[2]), .C(rcfg), .Q(d_ff_2_q[0]));  // open: nQ
  D_FF d_ff_3 (.D(d_ff_1_q[0]), .C(rcfg), .Q(d_ff_1_q[1]));  // open: nQ
  D_FF d_ff_4 (.D(d_ff_2_q[0]), .C(rcfg), .Q(d_ff_2_q[1]));  // open: nQ
  D_FF d_ff_5 (.D(d_ff_1_q[1]), .C(rcfg), .Q(d_ff_1_q[2]));  // open: nQ
  D_FF d_ff_6 (.D(d_ff_2_q[1]), .C(rcfg), .Q(scfg));  // open: nQ
  Multiplexer #(.Selector_Bits(3)) multiplexer_1 (
    .sel({scfg, d_ff_2_q}), .in_0(e0), .in_1(e1), .in_2(e2), .in_3(e3), .in_4(e4), .in_5(e5), .in_6(e6),
    .in_7(e7), .out(s0));
  Multiplexer #(.Selector_Bits(3)) multiplexer_2 (
    .sel(d_ff_1_q), .in_0(e0), .in_1(e1), .in_2(e2), .in_3(e3), .in_4(e4), .in_5(e5), .in_6(e6), .in_7(e7),
    .out(s1));
endmodule
