// Digital circuit rota4.dig as structural Verilog
module rota4 (
  input  el1,
  input  el0,
  input  eo1,
  input  eo0,
  input  en0,
  input  en1,
  input  es0,
  input  es1,
  input  rcfg,
  input  ecfg,
  input  d,
  input  q,
  output sl0,
  output sl1,
  output so0,
  output so1,
  output sn0,
  output sn1,
  output ss0,
  output ss1,
  output scfg
);

  wire rota1_1_scfg, rota1_2_scfg, rota1_3_scfg;

  rota1 rota1_1 (
    .e0(d), .e1(q), .e2(en0), .e3(en1), .e4(el0), .e5(el1), .e6(es0), .e7(es1), .ecfg(rota1_2_scfg),
    .rcfg(rcfg), .s0(so0), .s1(so1), .scfg(rota1_1_scfg));
  rota1 rota1_2 (
    .e0(d), .e1(q), .e2(el0), .e3(el1), .e4(es0), .e5(es1), .e6(eo0), .e7(eo1), .ecfg(ecfg), .rcfg(rcfg),
    .s0(sn0), .s1(sn1), .scfg(rota1_2_scfg));
  rota1 rota1_3 (
    .e0(d), .e1(q), .e2(eo0), .e3(eo1), .e4(en0), .e5(en1), .e6(el0), .e7(el1), .ecfg(rota1_1_scfg),
    .rcfg(rcfg), .s0(ss0), .s1(ss1), .scfg(rota1_3_scfg));
  rota1 rota1_4 (
    .e0(d), .e1(q), .e2(es0), .e3(es1), .e4(eo0), .e5(eo1), .e6(en0), .e7(en1), .ecfg(rota1_3_scfg),
    .rcfg(rcfg), .s0(sl0), .s1(sl1), .scfg(scfg));
endmodule
