// Digital circuit cnt4.dig as structural Verilog
module cnt4 (
  input  d0,
  input  d1,
  input  d2,
  input  d3,
  input  conta,
  input  carrega,
  input  relogio,
  input  [7:0] X,
  output s3,
  output s2,
  output s1,
  output s0,
  output fim,
  output [7:0] Z,
  output V
);

  wire add_1_s, add_2_c_o, add_2_s, add_3_c_o, add_3_s, add_4_c_o, add_4_s, multiplexer_1_out,
       multiplexer_2_out, multiplexer_3_out, multiplexer_4_out, multiplexer_5_out, multiplexer_6_out,
       multiplexer_7_out, multiplexer_8_out;
  wire [7:0] add_5_s, multiplexer_9_out, multiplexer_10_out;

  Multiplexer multiplexer_1 (.sel(conta), .in_0(s3), .in_1(add_1_s), .out(multiplexer_1_out));
  Multiplexer multiplexer_2 (.sel(conta), .in_0(s2), .in_1(add_2_s), .out(multiplexer_2_out));
  Multiplexer multiplexer_3 (.sel(conta), .in_0(s1), .in_1(add_3_s), .out(multiplexer_3_out));
  Multiplexer multiplexer_4 (.sel(conta), .in_0(s0), .in_1(add_4_s), .out(multiplexer_4_out));
  Multiplexer multiplexer_5 (.sel(carrega), .in_0(multiplexer_1_out), .in_1(d3), .out(multiplexer_5_out));
  Multiplexer multiplexer_6 (.sel(carrega), .in_0(multiplexer_2_out), .in_1(d2), .out(multiplexer_6_out));
  Multiplexer multiplexer_7 (.sel(carrega), .in_0(multiplexer_3_out), .in_1(d1), .out(multiplexer_7_out));
  Multiplexer multiplexer_8 (.sel(carrega), .in_0(multiplexer_4_out), .in_1(d0), .out(multiplexer_8_out));
  D_FF d_ff_1 (.D(multiplexer_5_out), .C(relogio), .Q(s3));  // open: nQ
  D_FF d_ff_2 (.D(multiplexer_6_out), .C(relogio), .Q(s2));  // open: nQ
  D_FF d_ff_3 (.D(multiplexer_7_out), .C(relogio), .Q(s1));  // open: nQ
  D_FF d_ff_4 (.D(multiplexer_8_out), .C(relogio), .Q(s0));  // open: nQ
  Add add_1 (.a(s3), .b(1'b0), .c_i(add_2_c_o), .s(add_1_s), .c_o(fim));
  Add add_2 (.a(s2), .b(1'b0), .c_i(add_3_c_o), .s(add_2_s), .c_o(add_2_c_o));
  Add add_3 (.a(s1), .b(1'b0), .c_i(add_4_c_o), .s(add_3_s), .c_o(add_3_c_o));
  Add add_4 (.a(s0), .b(1'b0), .c_i(1'b1), .s(add_4_s), .c_o(add_4_c_o));
  Multiplexer #(.Bits(8)) multiplexer_9 (.sel(conta), .in_0(Z), .in_1(add_5_s), .out(multiplexer_9_out));
  Multiplexer #(.Bits(8)) multiplexer_10 (.sel(carrega), .in_0(multiplexer_9_out), .in_1(X), .out(multiplexer_10_out));
  D_FF #(.Bits(8)) d_ff_5 (.D(multiplexer_10_out), .C(relogio), .Q(Z));  // open: nQ
  Add #(.Bits(8)) add_5 (.a(Z), .b({8{1'b0}}), .c_i(1'b1), .s(add_5_s), .c_o(V));
endmodule
