// Digital circuit cnt8.dig as structural Verilog
module cnt8 (
  input  relogio
);

  wire counter_1_ovf, counter_2_ovf, counter_3_ovf, counter_4_ovf, inicializa_out, not_1_out;
  wire [3:0] counter_1_out, counter_2_out, counter_3_out, counter_4_out;

  Reset #(.invertOutput("false")) inicializa (.out(inicializa_out));
  Counter #(.Bits(4)) counter_1 (
    .en(1'b1), .C(not_1_out), .clr(inicializa_out), .out(counter_1_out), .ovf(counter_1_ovf));
  Counter #(.Bits(4)) counter_2 (
    .en(1'b1), .C(relogio), .clr(inicializa_out), .out(counter_2_out), .ovf(counter_2_ovf));
  Seven_Seg_Hex seven_seg_hex_1 (.d(counter_1_out), .dp(counter_1_ovf));
  Seven_Seg_Hex seven_seg_hex_2 (.d(counter_2_out), .dp(counter_2_ovf));
  not not_1 (not_1_out, counter_2_out[3]);
  Counter #(.Bits(4)) counter_3 (
    .en(counter_4_ovf), .C(relogio), .clr(inicializa_out), .out(counter_3_out), .ovf(counter_3_ovf));
  Counter #(.Bits(4)) counter_4 (
    .en(1'b1), .C(relogio), .clr(inicializa_out), .out(counter_4_out), .ovf(counter_4_ovf));
  Seven_Seg_Hex seven_seg_hex_3 (.d(counter_3_out), .dp(counter_3_ovf));
  Seven_Seg_Hex seven_seg_hex_4 (.d(counter_4_out), .dp(counter_4_ovf));
endmodule
