// Digital circuit cnttst.dig as structural Verilog
module cnttst (
  input  [3:0] d,
  input  \relógio ,
  input  [7:0] x,
  output [3:0] s,
  output [7:0] z,
  output fim,
  output v
);

  wire carrega_out, conta_out;

  DipSwitch conta (.out(conta_out));
  Button carrega (.out(carrega_out));
  cnt4 cnt4_1 (
    .d0(d[0]), .d1(d[1]), .d2(d[2]), .d3(d[3]), .conta(conta_out), .carrega(carrega_out),
    .relogio(\relógio ), .X(x), .s3(s[3]), .s2(s[2]), .s1(s[1]), .s0(s[0]), .fim(fim), .Z(z), .V(v));
  // ScopeTrigger scopetrigger_1: pin names not known; wires that end beside it: \relógio 
endmodule
