// Digital circuit membit.dig as structural Verilog
module membit (
  input  D,
  input  W,
  input  R,
  output Q
);

  wire nand_1_out, nand_2_out, nand_3_out, nand_4_out;

  nand nand_1 (nand_1_out, W, ~D);  // NAnd
  nand nand_2 (nand_2_out, W, D);
  nand nand_3 (nand_3_out, nand_1_out, nand_4_out);
  nand nand_4 (nand_4_out, nand_2_out, nand_3_out);
  and and_1 (Q, R, nand_4_out);
endmodule
