// Digital circuit mult16x16.dig as structural Verilog
module mult16x16 (
  input  relogio,
  input  [15:0] X,
  input  [15:0] Y,
  input  mult,
  output [15:0] MH,
  output [15:0] ML,
  output pronto,
  output [3:0] cnt
);

  wire add_1_c_o, and_2_out, C, fim, multfsmcir_1_desl, multfsmcir_1_ha, multfsmcir_1_hm, multfsmcir_1_hq,
       multfsmcir_1_inicia;
  wire [15:0] add_1_s, and_1_out, and_3_out, c1p16_1_s, c1p16_2_s, M, multiplexer_1_out, multiplexer_2_out;

  c1p16 c1p16_1 (.e(ML[0]), .s(c1p16_1_s));
  assign and_1_out = M & c1p16_1_s;  // And and_1, 16 bits wide
  Add #(.Bits(16)) add_1 (.a(MH), .b(and_1_out), .c_i(1'b0), .s(add_1_s), .c_o(add_1_c_o));
  multfsmcir multfsmcir_1 (
    .fim(fim), .mult(mult), .C(relogio), .desl(multfsmcir_1_desl), .hA(multfsmcir_1_ha),
    .hM(multfsmcir_1_hm), .hQ(multfsmcir_1_hq), .inicia(multfsmcir_1_inicia), .pronto(pronto));
  Multiplexer #(.Bits(16)) multiplexer_1 (
    .sel(multfsmcir_1_desl), .in_0(add_1_s), .in_1({C, MH[15:1]}), .out(multiplexer_1_out));
  c1p16 c1p16_2 (.e(multfsmcir_1_inicia), .s(c1p16_2_s));
  and and_2 (and_2_out, add_1_c_o, ~multfsmcir_1_inicia);  // And
  assign and_3_out = multiplexer_1_out & ~c1p16_2_s;  // And and_3, 16 bits wide
  Multiplexer #(.Bits(16)) multiplexer_2 (
    .sel(multfsmcir_1_desl), .in_0(X), .in_1({MH[0], ML[15:1]}), .out(multiplexer_2_out));
  Register u_C (.D(and_2_out), .C(relogio), .en(multfsmcir_1_ha), .Q(C));
  Register #(.Bits(16)) A (.D(and_3_out), .C(relogio), .en(multfsmcir_1_ha), .Q(MH));
  Register #(.Bits(16)) Q (.D(multiplexer_2_out), .C(relogio), .en(multfsmcir_1_hq), .Q(ML));
  Register #(.Bits(16)) u_M (.D(Y), .C(relogio), .en(multfsmcir_1_hm), .Q(M));
  Counter #(.Bits(4)) counter_1 (.en(multfsmcir_1_desl), .C(relogio), .clr(multfsmcir_1_inicia), .out(cnt), .ovf(fim));

  // Other names for the same wires on the sheet: A[15:0] = MH; Q[15:0] = ML

  // Notes on the sheet:
  //   Ciclo N-1
  //   Ciclo N
  //   Ciclo N+1
endmodule
