// Digital circuit multfsmcir.dig as structural Verilog
module multfsmcir (
  input  fim,
  input  mult,
  input  C,
  output desl,
  output hA,
  output hM,
  output hQ,
  output inicia,
  output pronto
);

  wire and_1_out, and_2_out, and_3_out, and_4_out, and_5_out, and_6_out, not_1_out, not_2_out, not_3_out,
       not_4_out, or_2_out, or_3_out, Z_1_n, Z_2_n;

  not not_1 (not_1_out, fim);
  not not_2 (not_2_out, Z_2_n);
  not not_3 (not_3_out, Z_1_n);
  not not_4 (not_4_out, hQ);
  and and_1 (and_1_out, hQ, Z_1_n, fim);
  and and_2 (and_2_out, hQ, not_3_out);
  and and_3 (and_3_out, not_4_out, Z_1_n);
  and and_4 (and_4_out, hQ, not_1_out);
  and and_5 (and_5_out, not_4_out, not_2_out, mult);
  and and_6 (and_6_out, not_4_out, Z_1_n);
  and and_7 (desl, hQ, Z_1_n);
  or or_1 (hA, hQ, Z_1_n, Z_2_n);
  and and_8 (hM, hQ, not_3_out);
  and and_9 (inicia, hQ, not_3_out);
  and and_10 (pronto, not_4_out, not_3_out, not_2_out);
  or or_2 (or_2_out, and_2_out, and_3_out, and_4_out);
  or or_3 (or_3_out, and_5_out, and_6_out);
  D_FF u_Z_2_n (.D(and_1_out), .C(C), .Q(Z_2_n));  // open: nQ
  D_FF u_Z_1_n (.D(or_2_out), .C(C), .Q(Z_1_n));  // open: nQ
  D_FF Z_0_n (.D(or_3_out), .C(C), .Q(hQ));  // open: nQ
  // Probe multfsm.fsm on {Z_2_n, Z_1_n, hQ}

  // Other names for the same wires on the sheet: Z_0_n = hQ

  // Notes on the sheet:
  //   C: Hz: 2
endmodule
