// Digital circuit parcir.dig as structural Verilog
module parcir (
  input  n,
  input  C,
  output s
);

  wire and_1_out, and_2_out, not_1_out, or_1_out, Z_0_n;

  not not_1 (not_1_out, n);
  not not_2 (s, Z_0_n);
  and and_1 (and_1_out, s, n);
  and and_2 (and_2_out, Z_0_n, not_1_out);
  or or_1 (or_1_out, and_1_out, and_2_out);
  D_FF u_Z_0_n (.D(or_1_out), .C(C), .Q(Z_0_n));  // open: nQ
  // Probe par.fsm on Z_0_n

  // Notes on the sheet:
  //   C: Hz: 2
endmodule
