// Digital circuit ram4x6.dig as structural Verilog
module ram4x6 (
  input  [1:0] endereco,
  input  escrita,
  input  leitura,
  input  [5:0] Dentrada,
  output [5:0] Dsaida
);

  wire and_1_out, and_2_out, and_3_out, and_4_out, and_5_out, and_6_out, and_7_out, and_8_out, and_9_out,
       and_10_out, and_11_out, and_12_out, membit_1_q, membit_2_q, membit_3_q, membit_4_q, membit_5_q,
       membit_6_q, membit_7_q, membit_8_q, membit_9_q, membit_10_q, membit_11_q, membit_12_q, membit_13_q,
       membit_14_q, membit_15_q, membit_16_q, membit_17_q, membit_18_q, membit_19_q, membit_20_q,
       membit_21_q, membit_22_q, membit_23_q, membit_24_q, nfet_1_d, nfet_5_d, nfet_9_d, nfet_13_d,
       nfet_17_d, nfet_21_d;

  and and_1 (and_1_out, ~endereco[1], ~endereco[0]);  // And
  and and_2 (and_2_out, ~endereco[1], endereco[0]);  // And
  and and_3 (and_3_out, endereco[1], ~endereco[0]);  // And
  and and_4 (and_4_out, endereco[1], endereco[0]);
  and and_5 (and_5_out, and_1_out, escrita);
  and and_6 (and_6_out, and_1_out, leitura);
  and and_7 (and_7_out, and_2_out, escrita);
  and and_8 (and_8_out, and_2_out, leitura);
  and and_9 (and_9_out, and_3_out, escrita);
  and and_10 (and_10_out, and_3_out, leitura);
  and and_11 (and_11_out, and_4_out, escrita);
  and and_12 (and_12_out, and_4_out, leitura);
  membit membit_1 (.D(Dentrada[5]), .W(and_5_out), .R(and_6_out), .Q(membit_1_q));
  membit membit_2 (.D(Dentrada[5]), .W(and_7_out), .R(and_8_out), .Q(membit_2_q));
  membit membit_3 (.D(Dentrada[5]), .W(and_9_out), .R(and_10_out), .Q(membit_3_q));
  membit membit_4 (.D(Dentrada[5]), .W(and_11_out), .R(and_12_out), .Q(membit_4_q));
  NFET nfet_1 (.G(membit_1_q), .D(nfet_1_d), .S(1'b0));
  NFET nfet_2 (.G(membit_2_q), .D(nfet_1_d), .S(1'b0));
  NFET nfet_3 (.G(membit_3_q), .D(nfet_1_d), .S(1'b0));
  NFET nfet_4 (.G(membit_4_q), .D(nfet_1_d), .S(1'b0));
  PullUp pullup_1 (.out(nfet_1_d));
  membit membit_5 (.D(Dentrada[4]), .W(and_5_out), .R(and_6_out), .Q(membit_5_q));
  membit membit_6 (.D(Dentrada[4]), .W(and_7_out), .R(and_8_out), .Q(membit_6_q));
  membit membit_7 (.D(Dentrada[4]), .W(and_9_out), .R(and_10_out), .Q(membit_7_q));
  membit membit_8 (.D(Dentrada[4]), .W(and_11_out), .R(and_12_out), .Q(membit_8_q));
  NFET nfet_5 (.G(membit_5_q), .D(nfet_5_d), .S(1'b0));
  NFET nfet_6 (.G(membit_6_q), .D(nfet_5_d), .S(1'b0));
  NFET nfet_7 (.G(membit_7_q), .D(nfet_5_d), .S(1'b0));
  NFET nfet_8 (.G(membit_8_q), .D(nfet_5_d), .S(1'b0));
  PullUp pullup_2 (.out(nfet_5_d));
  membit membit_9 (.D(Dentrada[3]), .W(and_5_out), .R(and_6_out), .Q(membit_9_q));
  membit membit_10 (.D(Dentrada[3]), .W(and_7_out), .R(and_8_out), .Q(membit_10_q));
  membit membit_11 (.D(Dentrada[3]), .W(and_9_out), .R(and_10_out), .Q(membit_11_q));
  membit membit_12 (.D(Dentrada[3]), .W(and_11_out), .R(and_12_out), .Q(membit_12_q));
  NFET nfet_9 (.G(membit_9_q), .D(nfet_9_d), .S(1'b0));
  NFET nfet_10 (.G(membit_10_q), .D(nfet_9_d), .S(1'b0));
  NFET nfet_11 (.G(membit_11_q), .D(nfet_9_d), .S(1'b0));
  NFET nfet_12 (.G(membit_12_q), .D(nfet_9_d), .S(1'b0));
  PullUp pullup_3 (.out(nfet_9_d));
  membit membit_13 (.D(Dentrada[2]), .W(and_5_out), .R(and_6_out), .Q(membit_13_q));
  membit membit_14 (.D(Dentrada[2]), .W(and_7_out), .R(and_8_out), .Q(membit_14_q));
  membit membit_15 (.D(Dentrada[2]), .W(and_9_out), .R(and_10_out), .Q(membit_15_q));
  membit membit_16 (.D(Dentrada[2]), .W(and_11_out), .R(and_12_out), .Q(membit_16_q));
  NFET nfet_13 (.G(membit_13_q), .D(nfet_13_d), .S(1'b0));
  NFET nfet_14 (.G(membit_14_q), .D(nfet_13_d), .S(1'b0));
  NFET nfet_15 (.G(membit_15_q), .D(nfet_13_d), .S(1'b0));
  NFET nfet_16 (.G(membit_16_q), .D(nfet_13_d), .S(1'b0));
  PullUp pullup_4 (.out(nfet_13_d));
  membit membit_17 (.D(Dentrada[1]), .W(and_5_out), .R(and_6_out), .Q(membit_17_q));
  membit membit_18 (.D(Dentrada[1]), .W(and_7_out), .R(and_8_out), .Q(membit_18_q));
  membit membit_19 (.D(Dentrada[1]), .W(and_9_out), .R(and_10_out), .Q(membit_19_q));
  membit membit_20 (.D(Dentrada[1]), .W(and_11_out), .R(and_12_out), .Q(membit_20_q));
  NFET nfet_17 (.G(membit_17_q), .D(nfet_17_d), .S(1'b0));
  NFET nfet_18 (.G(membit_18_q), .D(nfet_17_d), .S(1'b0));
  NFET nfet_19 (.G(membit_19_q), .D(nfet_17_d), .S(1'b0));
  NFET nfet_20 (.G(membit_20_q), .D(nfet_17_d), .S(1'b0));
  PullUp pullup_5 (.out(nfet_17_d));
  membit membit_21 (.D(Dentrada[0]), .W(and_5_out), .R(and_6_out), .Q(membit_21_q));
  membit membit_22 (.D(Dentrada[0]), .W(and_7_out), .R(and_8_out), .Q(membit_22_q));
  membit membit_23 (.D(Dentrada[0]), .W(and_9_out), .R(and_10_out), .Q(membit_23_q));
  membit membit_24 (.D(Dentrada[0]), .W(and_11_out), .R(and_12_out), .Q(membit_24_q));
  NFET nfet_21 (.G(membit_21_q), .D(nfet_21_d), .S(1'b0));
  NFET nfet_22 (.G(membit_22_q), .D(nfet_21_d), .S(1'b0));
  NFET nfet_23 (.G(membit_23_q), .D(nfet_21_d), .S(1'b0));
  NFET nfet_24 (.G(membit_24_q), .D(nfet_21_d), .S(1'b0));
  PullUp pullup_6 (.out(nfet_21_d));
  not not_1 (Dsaida[0], nfet_21_d);
  not not_2 (Dsaida[1], nfet_17_d);
  not not_3 (Dsaida[2], nfet_13_d);
  not not_4 (Dsaida[3], nfet_9_d);
  not not_5 (Dsaida[4], nfet_5_d);
  not not_6 (Dsaida[5], nfet_1_d);
endmodule
