// Digital circuit ringosc5.dig as structural Verilog
module ringosc5 (
  input  R,
  output C
);

  wire nor_1_out, not_1_out, not_2_out, not_3_out;

  nor nor_1 (nor_1_out, R, C);
  not not_1 (not_1_out, nor_1_out);
  not not_2 (not_2_out, not_1_out);
  not not_3 (not_3_out, not_2_out);
  not not_4 (C, not_3_out);
endmodule
