// Digital circuit sj_digital.dig as structural Verilog
module sj_digital (
  input  clock50Mhz,
  input  [41:0] dreqo,
  input  drspo,
  output [15:0] left,
  output [15:0] right,
  output [34:0] drspi,
  output dreqi,
  output [11:0] X,
  output [11:0] Y,
  output DE,
  output ACLK,
  output CYC
);

  wire and_1_out, and_2_out, and_3_out, and_4_out, and_5_out, and_6_out, and_7_out, and_8_out, and_9_out,
       and_10_out, and_12_out, d_ff_1_nq, d_ff_1_q, d_ff_2_nq, demultiplexer_1_out_0, p1__button1,
       p1__button2, p1__button3, p1__button4, p1__button5, p1__button6, p1__down, p1__left, p1__right,
       p1__select, p1__start, p1__up, p2__button1, p2__button2, p2__button3, p2__button4, p2__button5,
       p2__button6, p2__down, p2__left, p2__right, p2__select, p2__start, p2__up, resetn, v__b, v__clk, v__g,
       v__hs, v__r, v__vs, wb__ack, wb__we;
  wire [3:0] wb__sel;
  wire [7:0] caracter, mem0d, mem1d, mem2d, mem3d;
  wire [15:0] led, switch, teclado_d;
  wire [31:0] wb__adr, wb__dat__master, wb__dat__slave;
  wire [63:0] seg;

  Button button_1 (.out(p1__up));
  Button button_2 (.out(p1__left));
  Button button_3 (.out(p1__down));
  Button button_4 (.out(p2__up));
  Button button_5 (.out(p2__left));
  Button button_6 (.out(p2__down));
  Button button_7 (.out(p1__right));
  Button button_8 (.out(p2__right));
  Reset u_resetn (.out(resetn));
  Button button_9 (.out(p1__select));
  Button button_10 (.out(p1__button1));
  Button button_11 (.out(p1__button2));
  Button button_12 (.out(p1__button3));
  Button button_13 (.out(p1__button4));
  Button button_14 (.out(p1__button5));
  Button button_15 (.out(p1__button6));
  Button button_16 (.out(p2__select));
  Button button_17 (.out(p2__button1));
  Button button_18 (.out(p2__button2));
  Button button_19 (.out(p2__button3));
  Button button_20 (.out(p2__button4));
  Button button_21 (.out(p2__button5));
  Button button_22 (.out(p2__button6));
  Button button_23 (.out(p1__start));
  Button button_24 (.out(p2__start));
  and and_1 (and_1_out, wb__adr[28], wb__adr[29], wb__adr[30], wb__adr[31]);
  and and_2 (and_2_out, and_1_out, wb__ack);
  Demultiplexer #(.Selector_Bits(4)) demultiplexer_1 (
    .sel(wb__adr[27:24]), .in(and_2_out), .out_0(demultiplexer_1_out_0));  // open: out_1, out_2, out_3, out_4, out_5, out_6, out_7, out_8, out_9, out_10, out_11, out_12, out_13, out_14, out_15
  // vg vg_1: pin names not known; wires that end beside it: clock50Mhz, resetn, p1__select, p1__start, p1__up, p1__down, p1__left, p1__right, p1__button1, p1__button2, p1__button3, p1__button4, p1__button5, p1__button6, p2__select, p2__start, p2__up, p2__down, p2__left, p2__right, p2__button1, p2__button2, p2__button3, p2__button4, p2__button5, p2__button6, switch, wb__dat__slave, wb__ack, dreqo[0], dreqo[7:1], v__r, v__g, v__b, v__vs, v__hs, v__clk, X, Y, DE, left, right, ACLK, led, seg, wb__adr
  Multiplexer #(.Bits(32)) multiplexer_1 (
    .sel(and_1_out), .in_0({mem3d, mem2d, mem1d, mem0d}), .in_1({{24{1'b0}}, caracter}), .out(wb__dat__slave));
  and and_3 (and_3_out, wb__ack, wb__we, wb__sel[0]);
  and and_4 (and_4_out, wb__ack, ~wb__we, wb__sel[0]);  // And
  and and_5 (and_5_out, wb__ack, wb__we, wb__sel[1]);
  and and_6 (and_6_out, wb__ack, ~wb__we, wb__sel[1]);  // And
  and and_7 (and_7_out, wb__ack, wb__we, wb__sel[2]);
  and and_8 (and_8_out, wb__ack, ~wb__we, wb__sel[2]);  // And
  and and_9 (and_9_out, wb__ack, wb__we, wb__sel[3]);
  and and_10 (and_10_out, wb__ack, ~wb__we, wb__sel[3]);  // And
  Seven_Seg seven_seg_1 (
    .a(seg[63]), .b(seg[62]), .c(seg[61]), .d(seg[60]), .e(seg[59]), .f(seg[58]), .g(seg[57]), .dp(seg[56]));
  VGA video (.R(v__r), .G(v__g), .B(v__b), .H(v__hs), .V(v__vs), .C(v__clk));
  DipSwitch sw0 (.out(switch[0]));
  DipSwitch sw1 (.out(switch[1]));
  DipSwitch sw2 (.out(switch[2]));
  DipSwitch sw3 (.out(switch[3]));
  DipSwitch sw4 (.out(switch[4]));
  DipSwitch sw5 (.out(switch[5]));
  DipSwitch sw6 (.out(switch[6]));
  DipSwitch sw7 (.out(switch[7]));
  DipSwitch sw8 (.out(switch[8]));
  DipSwitch sw9 (.out(switch[9]));
  DipSwitch sw10 (.out(switch[10]));
  DipSwitch sw11 (.out(switch[11]));
  DipSwitch sw12 (.out(switch[12]));
  DipSwitch sw13 (.out(switch[13]));
  DipSwitch sw14 (.out(switch[14]));
  DipSwitch sw15 (.out(switch[15]));
  Seven_Seg seven_seg_2 (
    .a(seg[55]), .b(seg[54]), .c(seg[53]), .d(seg[52]), .e(seg[51]), .f(seg[50]), .g(seg[49]), .dp(seg[48]));
  Keyboard teclado (.C(clock50Mhz), .en(demultiplexer_1_out_0), .D(teclado_d));  // open: av
  D_FF d_ff_1 (.D(wb__ack), .C(clock50Mhz), .Q(d_ff_1_q), .nQ(d_ff_1_nq));
  Seven_Seg seven_seg_3 (
    .a(seg[47]), .b(seg[46]), .c(seg[45]), .d(seg[44]), .e(seg[43]), .f(seg[42]), .g(seg[41]), .dp(seg[40]));
  and and_11 (demultiplexer_1_out_0, d_ff_1_nq, wb__ack);
  D_FF d_ff_2 (.D(d_ff_1_q), .C(clock50Mhz), .nQ(d_ff_2_nq));  // open: Q
  LED led0 (.in(led[0]));
  LED led1 (.in(led[1]));
  LED led2 (.in(led[2]));
  LED led3 (.in(led[3]));
  LED led4 (.in(led[4]));
  LED led5 (.in(led[5]));
  LED led6 (.in(led[6]));
  LED led7 (.in(led[7]));
  LED led8 (.in(led[8]));
  LED led9 (.in(led[9]));
  LED led10 (.in(led[10]));
  LED led11 (.in(led[11]));
  LED led12 (.in(led[12]));
  LED led13 (.in(led[13]));
  LED led14 (.in(led[14]));
  LED led15 (.in(led[15]));
  Seven_Seg seven_seg_4 (
    .a(seg[39]), .b(seg[38]), .c(seg[37]), .d(seg[36]), .e(seg[35]), .f(seg[34]), .g(seg[33]), .dp(seg[32]));
  and and_12 (and_12_out, d_ff_2_nq, d_ff_1_q);
  RAMDualPort #(.AddrBits(16), .Bits(8)) Mem0 (
    .A(wb__adr[17:2]), .Din(wb__dat__master[7:0]), .str(and_3_out), .C(clock50Mhz), .ld(and_4_out), .D(mem0d));
  RAMDualPort #(.AddrBits(16), .Bits(8)) Mem1 (
    .A(wb__adr[17:2]), .Din(wb__dat__master[15:8]), .str(and_5_out), .C(clock50Mhz), .ld(and_6_out), .D(mem1d));
  RAMDualPort #(.AddrBits(16), .Bits(8)) Mem2 (
    .A(wb__adr[17:2]), .Din(wb__dat__master[23:16]), .str(and_7_out), .C(clock50Mhz), .ld(and_8_out),
    .D(mem2d));
  RAMDualPort #(.AddrBits(16), .Bits(8)) Mem3 (
    .A(wb__adr[17:2]), .Din(wb__dat__master[31:24]), .str(and_9_out), .C(clock50Mhz), .ld(and_10_out),
    .D(mem3d));
  Seven_Seg seven_seg_5 (
    .a(seg[31]), .b(seg[30]), .c(seg[29]), .d(seg[28]), .e(seg[27]), .f(seg[26]), .g(seg[25]), .dp(seg[24]));
  Register #(.Bits(8)) u_caracter (.D({1'b0, teclado_d[6:0]}), .C(clock50Mhz), .en(and_12_out), .Q(caracter));
  Seven_Seg seven_seg_6 (
    .a(seg[23]), .b(seg[22]), .c(seg[21]), .d(seg[20]), .e(seg[19]), .f(seg[18]), .g(seg[17]), .dp(seg[16]));
  Seven_Seg seven_seg_7 (
    .a(seg[15]), .b(seg[14]), .c(seg[13]), .d(seg[12]), .e(seg[11]), .f(seg[10]), .g(seg[9]), .dp(seg[8]));
  Seven_Seg seven_seg_8 (
    .a(seg[7]), .b(seg[6]), .c(seg[5]), .d(seg[4]), .e(seg[3]), .f(seg[2]), .g(seg[1]), .dp(seg[0]));

  // Other names for the same wires on the sheet: a__clk = ACLK; a__left[15:0] = left; a__right[15:0] = right;
  //   dmi__req__ready = dreqi; dmi__rsp__data[31:0] = drspi[32:1]; dmi__rsp__op[1:0] = drspi[34:33];
  //   dmi__rsp__ready = drspo; dmi__rsp__valid = drspi[0]; dmi__req__valid = dreqo[0];
  //   dmi__req__address[6:0] = dreqo[7:1]; dmi__req__data[31:0] = dreqo[39:8]; dmi__req__op[1:0] = dreqo[41:40];
  //   v__de = DE; v__x[11:0] = X; v__y[11:0] = Y; wb__cyc = CYC; wb__stb = wb__ack

  // Notes on the sheet:
  //   clock50Mhz: Hz: 2147483647
  //   Depuração
  //   sistema
  //   Jogador
  //   Wishbone
  //   Mapa de memória Wishbone:
  //      0x00000000 a 0xEFFFFFFF memória externa
  //      0xF0000000 a 0xF0FFFFFF teclado
  //      0xF1000000 a 0xF1FFFFFF cartão SD
  //   AV
  //   Entradas e Saídas Simples
  //   Teclado
  //   Memória Externa
  //   256KB (64K palavras)
  //   0x00000000  a
  //   0x0003FFFF
  //   e repetindo até
  //   0xEFFFFFFF
endmodule
