// Digital circuit compara.dig as structural Verilog
// Compara dois números de 12 bits e indica se são iguais
module compara (
  input  [11:0] A,
  input  [11:0] B,
  output eq
);

  wire [11:0] xor_1_out;

  assign xor_1_out = A ^ B;  // XOr xor_1, 12 bits wide
  nor nor_1 (eq, xor_1_out[0], xor_1_out[1], xor_1_out[2], xor_1_out[3], xor_1_out[4], xor_1_out[5], xor_1_out[6], xor_1_out[7], xor_1_out[8], xor_1_out[9], xor_1_out[10], xor_1_out[11]);
endmodule
