// Digital circuit jogo.dig as structural Verilog
// Todo o estado que representa o jogo (placares, posicoes dos jogadores
// e posicao da bola) eh modificado neste bloco de acordo com os
// sinais vindo da entrada. Este pode ser um circuito muito lento jah
// que nao adianta modificar o estado mais que uma vez por imagem de
// video, que eh atualizado umas 60 vezes por segundo
module jogo (
  input  relogio,
  input  inicializa,
  input  vs,
  input  sobe1,
  input  desce1,
  input  sobe2,
  input  desce2,
  input  colj1,
  input  colj2,
  output [11:0] bolax,
  output [11:0] bolay,
  output [11:0] j1y,
  output [11:0] j2y,
  output [3:0] digito1,
  output [3:0] digito10,
  output [3:0] digito2,
  output [3:0] digito20
);

  wire and_1_out, and_2_out, and_3_out, and_4_out, and_5_out, and_6_out, and_7_out, and_8_out, and_9_out,
       and_10_out, and_11_out, comparator_1_lt, comparator_2_gt, comparator_3_lt, comparator_4_gt, d_ff_1_nq,
       ffsr_1_q, ffsr_2_q, nor_1_out, or_1_out, or_2_out, or_4_out, or_5_out, rebate, xdir;

  and and_1 (and_1_out, rebate, or_1_out);
  or or_1 (or_1_out, and_2_out, and_3_out);
  and and_2 (and_2_out, ffsr_2_q, desce2);
  and and_3 (and_3_out, ffsr_1_q, desce1);
  D_FF d_ff_1 (.D(vs), .C(relogio), .nQ(d_ff_1_nq));  // open: Q
  and and_4 (and_4_out, rebate, or_2_out);
  or or_2 (or_2_out, and_5_out, and_6_out);
  and and_5 (and_5_out, ffsr_2_q, sobe2);
  nor nor_1 (nor_1_out, d_ff_1_nq, vs);
  ffsr ffsr_1 (.S(colj1), .R(nor_1_out), .Q(ffsr_1_q));  // open: nQ
  ffsr ffsr_2 (.S(colj2), .R(nor_1_out), .Q(ffsr_2_q));  // open: nQ
  and and_6 (and_6_out, ffsr_1_q, sobe1);
  and and_7 (and_7_out, vs, d_ff_1_nq);
  and and_8 (and_8_out, ffsr_1_q, xdir);
  and and_9 (and_9_out, ffsr_2_q, ~xdir);  // And
  and and_10 (and_10_out, comparator_2_gt, and_7_out);
  and and_11 (and_11_out, comparator_1_lt, and_7_out);
  or or_3 (rebate, and_8_out, and_9_out);
  bola1d horizontal (
    .relogio(relogio), .inicializa(inicializa), .move(and_7_out), .centro(12'h140), .volta(or_5_out),
    .reflete(rebate), .sobe(1'b0), .desce(1'b0), .posicao(bolax), .dir(xdir));
  bola1d vertical (
    .relogio(relogio), .inicializa(inicializa), .move(and_7_out), .centro(12'hf0), .volta(or_5_out),
    .reflete(or_4_out), .sobe(and_4_out), .desce(and_1_out), .posicao(bolay));  // open: dir
  raquete raquete_1 (
    .relogio(relogio), .inicializa(inicializa), .move(and_7_out), .sobe(sobe1), .desce(desce1), .y(j1y));
  raquete raquete_2 (
    .relogio(relogio), .inicializa(inicializa), .move(and_7_out), .sobe(sobe2), .desce(desce2), .y(j2y));
  placar placar_1 (
    .relogio(relogio), .inicializa(inicializa), .conta(and_10_out), .digito1(digito1), .digito10(digito10));
  placar placar_2 (
    .relogio(relogio), .inicializa(inicializa), .conta(and_11_out), .digito1(digito2), .digito10(digito20));
  Comparator #(.Bits(12)) comparator_1 (.a(bolax), .b(12'h8), .lt(comparator_1_lt));  // open: gt, eq
  Comparator #(.Bits(12)) comparator_2 (.a(bolax), .b(12'h278), .gt(comparator_2_gt));  // open: eq, lt
  Comparator #(.Bits(12)) comparator_3 (.a(bolay), .b(12'h8), .lt(comparator_3_lt));  // open: gt, eq
  Comparator #(.Bits(12)) comparator_4 (.a(bolay), .b(12'h1d8), .gt(comparator_4_gt));  // open: eq, lt
  or or_4 (or_4_out, comparator_3_lt, comparator_4_gt);
  or or_5 (or_5_out, comparator_1_lt, comparator_2_gt);
endmodule
