// Digital circuit pintor.dig as structural Verilog
// Este bloco transforma o estado do jogo numa imagem visivel na tela usando
// a informacao das coordenadas x e y do ponto que esta sendo desenhado na
// tela neste instante.
module pintor (
  input  [11:0] x,
  input  [11:0] y,
  input  [11:0] bx,
  input  [11:0] by,
  input  [11:0] j1y,
  input  [11:0] j2y,
  input  [3:0] digito1,
  input  [3:0] digito10,
  input  [3:0] digito2,
  input  [3:0] digito20,
  output borda,
  output placar2,
  output jogador2,
  output placar1,
  output jogador1,
  output bola
);

  wire comparator_1_lt, comparator_2_gt, digito_1_caracter, digito_2_caracter, digito_3_caracter,
       digito_4_caracter, retangulo_1_r;
  wire [11:0] add_1_s, add_2_s, add_3_s, add_4_s, sub_1_s, sub_2_s, sub_3_s, sub_4_s;

  digito digito_1 (.x(x), .y(y), .digito(digito1), .pos(5'b00110), .caracter(digito_1_caracter));
  digito digito_2 (.x(x), .y(y), .digito(digito10), .pos(5'b00101), .caracter(digito_2_caracter));
  digito digito_3 (.x(x), .y(y), .digito(digito2), .pos(5'b01111), .caracter(digito_3_caracter));
  digito digito_4 (.x(x), .y(y), .digito(digito20), .pos(5'b01110), .caracter(digito_4_caracter));
  Sub #(.Bits(12)) sub_1 (.a(bx), .b(12'h6), .c_i(1'b0), .s(sub_1_s));  // open: c_o
  Sub #(.Bits(12)) sub_2 (.a(by), .b(12'h6), .c_i(1'b0), .s(sub_2_s));  // open: c_o
  Sub #(.Bits(12)) sub_3 (.a(j1y), .b(12'h28), .c_i(1'b0), .s(sub_3_s));  // open: c_o
  or or_1 (placar1, digito_1_caracter, digito_2_caracter);
  or or_2 (placar2, digito_3_caracter, digito_4_caracter);
  Add #(.Bits(12)) add_1 (.a(bx), .b(12'h6), .c_i(1'b0), .s(add_1_s));  // open: c_o
  Add #(.Bits(12)) add_2 (.a(by), .b(12'h6), .c_i(1'b0), .s(add_2_s));  // open: c_o
  Add #(.Bits(12)) add_3 (.a(j1y), .b(12'h28), .c_i(1'b0), .s(add_3_s));  // open: c_o
  Sub #(.Bits(12)) sub_4 (.a(j2y), .b(12'h28), .c_i(1'b0), .s(sub_4_s));  // open: c_o
  Add #(.Bits(12)) add_4 (.a(j2y), .b(12'h28), .c_i(1'b0), .s(add_4_s));  // open: c_o
  retangulo retangulo_1 (.x(x), .y(y), .xmin(12'h13c), .xmax(12'h144), .ymin(12'h1), .ymax(12'h1de), .r(retangulo_1_r));
  retangulo retangulo_2 (.x(x), .y(y), .xmin(sub_1_s), .xmax(add_1_s), .ymin(sub_2_s), .ymax(add_2_s), .r(bola));
  retangulo retangulo_3 (.x(x), .y(y), .xmin(12'h20), .xmax(12'h2e), .ymin(sub_3_s), .ymax(add_3_s), .r(jogador1));
  retangulo retangulo_4 (.x(x), .y(y), .xmin(12'h252), .xmax(12'h260), .ymin(sub_4_s), .ymax(add_4_s), .r(jogador2));
  Comparator #(.Bits(12)) comparator_1 (.a(y), .b(12'h8), .lt(comparator_1_lt));  // open: gt, eq
  Comparator #(.Bits(12)) comparator_2 (.a(y), .b(12'h1d8), .gt(comparator_2_gt));  // open: eq, lt
  or or_3 (borda, comparator_1_lt, retangulo_1_r, comparator_2_gt);
endmodule
