// Digital circuit pong.dig as structural Verilog
module pong (
  input  clk
);

  wire _1_out, _1_plus_out, _2_out, _2_plus_out, and_1_out, and_2_out, and_3_out, horizontal_fim,
       horizontal_mostra, horizontal_sinc, inicializa_out, not_1_out, not_2_out, not_3_out, pintor_1_bola,
       pintor_1_borda, pintor_1_jogador1, pintor_1_jogador2, pintor_1_placar1, pintor_1_placar2,
       vertical_mostra, vertical_sinc;
  wire [2:0] priorityencoder_1_num;
  wire [3:0] jogo_1_digito1, jogo_1_digito2, jogo_1_digito10, jogo_1_digito20;
  wire [11:0] horizontal_contagem, jogo_1_bolax, jogo_1_bolay, jogo_1_j1y, jogo_1_j2y, vertical_contagem;
  wire [23:0] multiplexer_1_out;

  Button inicializa (.out(inicializa_out));
  Button _1_plus (.out(_1_plus_out));
  Button _1 (.out(_1_out));
  Button _2_plus (.out(_2_plus_out));
  Button _2 (.out(_2_out));
  jogo jogo_1 (
    .relogio(clk), .inicializa(inicializa_out), .vs(vertical_sinc), .sobe1(_1_plus_out), .desce1(_1_out),
    .sobe2(_2_plus_out), .desce2(_2_out), .colj1(and_2_out), .colj2(and_3_out), .bolax(jogo_1_bolax),
    .bolay(jogo_1_bolay), .j1y(jogo_1_j1y), .j2y(jogo_1_j2y), .digito1(jogo_1_digito1),
    .digito10(jogo_1_digito10), .digito2(jogo_1_digito2), .digito20(jogo_1_digito20));
  temporiza vertical (
    .relogio(clk), .conta(horizontal_fim), .inicializa(inicializa_out), .upix(12'h1df), .inisinc(12'h1e9),
    .fimsinc(12'h1eb), .fimcont(12'h20c), .contagem(vertical_contagem), .mostra(vertical_mostra),
    .sinc(vertical_sinc));  // open: fim
  temporiza horizontal (
    .relogio(clk), .conta(1'b1), .inicializa(inicializa_out), .upix(12'h27f), .inisinc(12'h28f),
    .fimsinc(12'h2ef), .fimcont(12'h31f), .contagem(horizontal_contagem), .fim(horizontal_fim),
    .mostra(horizontal_mostra), .sinc(horizontal_sinc));
  pintor pintor_1 (
    .x(horizontal_contagem), .y(vertical_contagem), .bx(jogo_1_bolax), .by(jogo_1_bolay), .j1y(jogo_1_j1y),
    .j2y(jogo_1_j2y), .digito1(jogo_1_digito1), .digito10(jogo_1_digito10), .digito2(jogo_1_digito2),
    .digito20(jogo_1_digito20), .borda(pintor_1_borda), .placar2(pintor_1_placar2),
    .jogador2(pintor_1_jogador2), .placar1(pintor_1_placar1), .jogador1(pintor_1_jogador1),
    .bola(pintor_1_bola));
  not not_1 (not_1_out, vertical_sinc);
  not not_2 (not_2_out, horizontal_sinc);
  and and_1 (and_1_out, vertical_mostra, horizontal_mostra);
  and and_2 (and_2_out, pintor_1_bola, pintor_1_jogador1);
  and and_3 (and_3_out, pintor_1_bola, pintor_1_jogador2);
  not not_3 (not_3_out, and_1_out);
  PriorityEncoder #(.Selector_Bits(3)) priorityencoder_1 (
    .in0(1'b1), .in1(pintor_1_borda), .in2(pintor_1_placar2), .in3(pintor_1_jogador2),
    .in4(pintor_1_placar1), .in5(pintor_1_jogador1), .in6(pintor_1_bola), .in7(not_3_out),
    .num(priorityencoder_1_num));  // open: any
  VGA vga_1 (
    .R(multiplexer_1_out[7:0]), .G(multiplexer_1_out[15:8]), .B(multiplexer_1_out[23:16]), .H(not_2_out),
    .V(not_1_out), .C(clk));
  Multiplexer #(.Selector_Bits(3), .Bits(24)) multiplexer_1 (
    .sel(priorityencoder_1_num), .in_0(24'h8000), .in_1(24'hfff0ff), .in_2(24'hff7f00), .in_3(24'hff7f00),
    .in_4(24'h7fff), .in_5(24'h7fff), .in_6(24'hffff), .in_7({24{1'b0}}), .out(multiplexer_1_out));

  // Notes on the sheet:
  //   clk: Hz: 2147483647
  //   640x480 60Hz, 25.175MHz, 640, 16, 96, 48, 480, 11, 2, 31
endmodule
