// Digital circuit digito.dig as structural Verilog
module digito (
  input  [11:0] x,
  input  [11:0] y,
  input  [3:0] digito,
  input  [4:0] pos,
  output caracter
);

  wire _0_r, _1_r, _2_r, _3_r, _4_r, _5_r, _6_r, and_1_out, and_2_out, and_3_out, and_4_out, and_5_out,
       and_6_out, and_7_out, d0, d1, d2, d3, d4, d5, d6;

  ROM #(.AddrBits(4), .Bits(7)) hex2seg (.A(digito), .sel(1'b1), .D({d6, d5, d4, d3, d2, d1, d0}));
  retangulo _5 (
    .x(x), .y(y), .xmin({2'b00, pos, {5{1'b0}}}), .xmax({2'b00, pos, 5'b00010}), .ymin(12'h1e),
    .ymax(12'h2c), .r(_5_r));
  retangulo _4 (
    .x(x), .y(y), .xmin({2'b00, pos, {5{1'b0}}}), .xmax({2'b00, pos, 5'b00010}), .ymin(12'h2a),
    .ymax(12'h37), .r(_4_r));
  retangulo _0 (
    .x(x), .y(y), .xmin({2'b00, pos, {5{1'b0}}}), .xmax({2'b00, pos, 5'b01111}), .ymin(12'h1e),
    .ymax(12'h20), .r(_0_r));
  retangulo _6 (
    .x(x), .y(y), .xmin({2'b00, pos, {5{1'b0}}}), .xmax({2'b00, pos, 5'b01111}), .ymin(12'h2a),
    .ymax(12'h2c), .r(_6_r));
  retangulo _3 (
    .x(x), .y(y), .xmin({2'b00, pos, {5{1'b0}}}), .xmax({2'b00, pos, 5'b01111}), .ymin(12'h35),
    .ymax(12'h37), .r(_3_r));
  retangulo _1 (
    .x(x), .y(y), .xmin({2'b00, pos, 5'b01101}), .xmax({2'b00, pos, 5'b01111}), .ymin(12'h1e), .ymax(12'h2c),
    .r(_1_r));
  retangulo _2 (
    .x(x), .y(y), .xmin({2'b00, pos, 5'b01101}), .xmax({2'b00, pos, 5'b01111}), .ymin(12'h2a), .ymax(12'h37),
    .r(_2_r));
  and and_1 (and_1_out, _0_r, d0);
  and and_2 (and_2_out, _1_r, d1);
  and and_3 (and_3_out, _2_r, d2);
  and and_4 (and_4_out, _3_r, d3);
  and and_5 (and_5_out, _4_r, d4);
  and and_6 (and_6_out, _5_r, d5);
  and and_7 (and_7_out, _6_r, d6);
  or or_1 (caracter, and_1_out, and_2_out, and_3_out, and_4_out, and_5_out, and_6_out, and_7_out);

  // Other names for the same wires on the sheet: x1[9:5] = pos; x2[9:5] = pos; x3[9:5] = pos; x4[9:5] = pos

  // Notes on the sheet:
  //   contents of hex2seg (hex, n*v repeats v):
  //   3f,6,5b,4f,66,6d,7d,7,7f,6f,77,7c,39,5e,79,71
endmodule
