// Digital circuit ffsr.dig as structural Verilog
// Flip flop mais básico, que pode ligar ou desligar a saída
module ffsr (
  input  S,
  input  R,
  output Q,
  output nQ
);

  nor nor_1 (Q, R, nQ);
  nor nor_2 (nQ, Q, S);

  // Notes on the sheet:
  //   S: liga Q
  //   R: desliga Q
endmodule
