// Digital circuit placar.dig as structural Verilog
module placar (
  input  relogio,
  input  inicializa,
  input  conta,
  output [3:0] digito1,
  output [3:0] digito10
);

  wire and_1_out, or_1_out;

  or or_1 (or_1_out, and_1_out, inicializa);
  Counter #(.Bits(4)) counter_1 (.en(conta), .C(relogio), .clr(or_1_out), .out(digito1));  // open: ovf
  Counter #(.Bits(4)) counter_2 (.en(or_1_out), .C(relogio), .clr(inicializa), .out(digito10));  // open: ovf
  and and_1 (and_1_out, digito1[0], ~digito1[1], ~digito1[2], digito1[3], conta);  // And
endmodule
