// Digital circuit pong_sj.dig as structural Verilog
// Isto é a mesma coisa que pong.dig mas com pinos de entrada e saída no
// padrão Shin JAMMA mais um pino extra de relógio de pixel. Este pino é
// necessário se fora simulado no Digital com o adaptador Shin JAMMA. Mas
// o principal objetivo deste projeto é que seu Verilog exportado seja usado
// com adaptadores de placas de FPGA.
// O relógio de 50 MHz é dividido por 2 para este circuito. Não é a frequência
// exata do VGA mas funciona em qualquer monitor.
module pong_sj (
  input  p1start,
  input  p1up,
  input  p1down,
  input  p2up,
  input  p2down,
  input  clock50MHz,
  output [7:0] red,
  output [7:0] green,
  output [7:0] blue,
  output hsync,
  output vsync,
  output pixelclk
);

  wire and_1_out, and_2_out, and_3_out, horizontal_fim, horizontal_mostra, horizontal_sinc, not_3_out,
       pintor_1_bola, pintor_1_borda, pintor_1_jogador1, pintor_1_jogador2, pintor_1_placar1,
       pintor_1_placar2, vertical_mostra, vertical_sinc;
  wire [2:0] priorityencoder_1_num;
  wire [3:0] jogo_1_digito1, jogo_1_digito2, jogo_1_digito10, jogo_1_digito20;
  wire [11:0] horizontal_contagem, jogo_1_bolax, jogo_1_bolay, jogo_1_j1y, jogo_1_j2y, vertical_contagem;

  D_FF d_ff_1 (.D(pixelclk), .C(clock50MHz), .nQ(pixelclk));  // open: Q
  jogo jogo_1 (
    .relogio(pixelclk), .inicializa(p1start), .vs(vertical_sinc), .sobe1(p1up), .desce1(p1down),
    .sobe2(p2up), .desce2(p2down), .colj1(and_2_out), .colj2(and_3_out), .bolax(jogo_1_bolax),
    .bolay(jogo_1_bolay), .j1y(jogo_1_j1y), .j2y(jogo_1_j2y), .digito1(jogo_1_digito1),
    .digito10(jogo_1_digito10), .digito2(jogo_1_digito2), .digito20(jogo_1_digito20));
  temporiza vertical (
    .relogio(pixelclk), .conta(horizontal_fim), .inicializa(p1start), .upix(12'h1df), .inisinc(12'h1e9),
    .fimsinc(12'h1eb), .fimcont(12'h20c), .contagem(vertical_contagem), .mostra(vertical_mostra),
    .sinc(vertical_sinc));  // open: fim
  temporiza horizontal (
    .relogio(pixelclk), .conta(1'b1), .inicializa(p1start), .upix(12'h27f), .inisinc(12'h28f),
    .fimsinc(12'h2ef), .fimcont(12'h31f), .contagem(horizontal_contagem), .fim(horizontal_fim),
    .mostra(horizontal_mostra), .sinc(horizontal_sinc));
  pintor pintor_1 (
    .x(horizontal_contagem), .y(vertical_contagem), .bx(jogo_1_bolax), .by(jogo_1_bolay), .j1y(jogo_1_j1y),
    .j2y(jogo_1_j2y), .digito1(jogo_1_digito1), .digito10(jogo_1_digito10), .digito2(jogo_1_digito2),
    .digito20(jogo_1_digito20), .borda(pintor_1_borda), .placar2(pintor_1_placar2),
    .jogador2(pintor_1_jogador2), .placar1(pintor_1_placar1), .jogador1(pintor_1_jogador1),
    .bola(pintor_1_bola));
  not not_1 (vsync, vertical_sinc);
  not not_2 (hsync, horizontal_sinc);
  and and_1 (and_1_out, vertical_mostra, horizontal_mostra);
  and and_2 (and_2_out, pintor_1_bola, pintor_1_jogador1);
  and and_3 (and_3_out, pintor_1_bola, pintor_1_jogador2);
  not not_3 (not_3_out, and_1_out);
  PriorityEncoder #(.Selector_Bits(3)) priorityencoder_1 (
    .in0(1'b1), .in1(pintor_1_borda), .in2(pintor_1_placar2), .in3(pintor_1_jogador2),
    .in4(pintor_1_placar1), .in5(pintor_1_jogador1), .in6(pintor_1_bola), .in7(not_3_out),
    .num(priorityencoder_1_num));  // open: any
  Multiplexer #(.Selector_Bits(3), .Bits(24)) multiplexer_1 (
    .sel(priorityencoder_1_num), .in_0(24'h8000), .in_1(24'hfff0ff), .in_2(24'hff7f00), .in_3(24'hff7f00),
    .in_4(24'h7fff), .in_5(24'h7fff), .in_6(24'hffff), .in_7({24{1'b0}}), .out({blue, green, red}));

  // Other names for the same wires on the sheet: clk25MHz = pixelclk

  // Notes on the sheet:
  //   640x480 60Hz, 25.175MHz, 640, 16, 96, 48, 480, 11, 2, 31
endmodule
