// Digital circuit raquete.dig as structural Verilog
module raquete (
  input  relogio,
  input  inicializa,
  input  move,
  input  sobe,
  input  desce,
  output [11:0] y
);

  wire and_1_out, and_2_out, comparator_1_gt, comparator_2_lt, or_1_out;
  wire [1:0] or_2_out;
  wire [11:0] add_1_s, multiplexer_1_out, sub_1_s;

  or or_1 (or_1_out, inicializa, move);
  Sub #(.Bits(12)) sub_1 (.a(y), .b(12'h2), .c_i(1'b0), .s(sub_1_s));  // open: c_o
  Add #(.Bits(12)) add_1 (.a(y), .b(12'h2), .c_i(1'b0), .s(add_1_s));  // open: c_o
  and and_1 (and_1_out, sobe, comparator_1_gt);
  and and_2 (and_2_out, desce, comparator_2_lt);
  or or_2 (or_2_out[0], inicializa, and_1_out);
  or or_3 (or_2_out[1], inicializa, and_2_out);
  Multiplexer #(.Bits(12), .Selector_Bits(2)) multiplexer_1 (
    .sel(or_2_out), .in_0(y), .in_1(sub_1_s), .in_2(add_1_s), .in_3(12'hf0), .out(multiplexer_1_out));
  Register #(.Bits(12)) posicao (.D(multiplexer_1_out), .C(relogio), .en(or_1_out), .Q(y));
  Comparator #(.Bits(12)) comparator_1 (.a(y), .b(12'h28), .gt(comparator_1_gt));  // open: eq, lt
  Comparator #(.Bits(12)) comparator_2 (.a(y), .b(12'h1b8), .lt(comparator_2_lt));  // open: gt, eq
endmodule
