// Digital circuit vg.dig as structural Verilog
module vg (
  input  clock50MHz__i,
  input  resetn__i,
  input  p1__select__i,
  input  p1__start__i,
  input  p1__up__i,
  input  p1__down__i,
  input  p1__left__i,
  input  p1__right__i,
  input  p1__button1__i,
  input  p1__button2__i,
  input  p1__button3__i,
  input  p1__button4__i,
  input  p1__button5__i,
  input  p1__button6__i,
  input  p2__select__i,
  input  p2__start__i,
  input  p2__up__i,
  input  p2__down__i,
  input  p2__left__i,
  input  p2__right__i,
  input  p2__button1__i,
  input  p2__button2__i,
  input  p2__button3__i,
  input  p2__button4__i,
  input  p2__button5__i,
  input  p2__button6__i,
  input  [15:0] switch__i,
  input  [31:0] wb__data__i,
  input  wb__ack__i,
  input  dmi__req__valid__i,
  input  [6:0] dmi__req__address__i,
  input  [31:0] dmi__req__data__i,
  input  [1:0] dmi__req__op__i,
  input  dmi__rsp__ready__i,
  output [7:0] v__r__o,
  output [7:0] v__g__o,
  output [7:0] v__b__o,
  output v__vs__o,
  output v__hs__o,
  output v__clk__o,
  output [11:0] v__x__o,
  output [11:0] v__y__o,
  output v__de__o,
  output [15:0] a__left__o,
  output [15:0] a__right__o,
  output a__clk__o,
  output [15:0] led__o,
  output [63:0] seg_o,
  output [31:0] wb__adr__o,
  output [31:0] wb__dat__o,
  output wb__we__o,
  output [3:0] wb__sel__o,
  output wb__stb__o,
  output wb__cyc__o,
  output dmi__req__ready__o,
  output dmi__rsp__valid__o,
  output [31:0] dmi__rsp__data__o,
  output [1:0] dmi__rsp__op__o
);

  wire and_1_out, and_2_out, and_3_out, and_5_out, and_6_out, d_ff_3_q, d_ff_4_q, horizontal_fim,
       horizontal_mostra, horizontal_sinc, jogo_1_a__rebate, jogo_1_a__reflete, jogo_1_a__torcida, not_3_out,
       or_1_out, or_2_out, or_3_out, pintor_1_bola, pintor_1_borda, pintor_1_jogador1, pintor_1_jogador2,
       pintor_1_placar1, pintor_1_placar2, vertical_mostra, vertical_sinc;
  wire [2:0] priorityencoder_1_num;
  wire [3:0] jogo_1_digito1, jogo_1_digito2, jogo_1_digito10, jogo_1_digito20;
  wire [11:0] jogo_1_bolax, jogo_1_bolay, jogo_1_j1y, jogo_1_j2y;
  wire [14:0] xnor_1_out;
  wire [14:14] d_ff_2_q;

  or or_1 (or_1_out, ~resetn__i, p1__start__i);  // Or
  or or_2 (or_2_out, p1__button1__i, p2__up__i);
  or or_3 (or_3_out, p1__button2__i, p2__down__i);
  D_FF d_ff_1 (.D(v__clk__o), .C(clock50MHz__i), .nQ(v__clk__o));  // open: Q
  jogo jogo_1 (
    .relogio(v__clk__o), .inicializa(or_1_out), .vs(vertical_sinc), .sobe1(p1__up__i), .desce1(p1__down__i),
    .sobe2(or_2_out), .desce2(or_3_out), .colj1(d_ff_3_q), .colj2(d_ff_4_q), .bolax(jogo_1_bolax),
    .bolay(jogo_1_bolay), .j1y(jogo_1_j1y), .j2y(jogo_1_j2y), .digito1(jogo_1_digito1),
    .digito10(jogo_1_digito10), .digito2(jogo_1_digito2), .digito20(jogo_1_digito20),
    .a__rebate(jogo_1_a__rebate), .a__reflete(jogo_1_a__reflete), .a__torcida(jogo_1_a__torcida));
  temporiza vertical (
    .relogio(v__clk__o), .conta(horizontal_fim), .inicializa(or_1_out), .upix(12'h1df), .inisinc(12'h1e9),
    .fimsinc(12'h1eb), .fimcont(12'h20c), .contagem({v__y__o[11:1], a__clk__o}), .mostra(vertical_mostra),
    .sinc(vertical_sinc));  // open: fim
  temporiza horizontal (
    .relogio(v__clk__o), .conta(1'b1), .inicializa(or_1_out), .upix(12'h27f), .inisinc(12'h28f),
    .fimsinc(12'h2ef), .fimcont(12'h31f), .contagem(v__x__o), .fim(horizontal_fim),
    .mostra(horizontal_mostra), .sinc(horizontal_sinc));
  and and_1 (and_1_out, v__y__o[4], jogo_1_a__rebate);
  and and_2 (and_2_out, v__y__o[2], jogo_1_a__reflete);
  and and_3 (and_3_out, xnor_1_out[0], jogo_1_a__torcida);
  not not_1 (v__vs__o, vertical_sinc);
  not not_2 (v__hs__o, horizontal_sinc);
  pintor pintor_1 (
    .x(v__x__o), .y({v__y__o[11:1], a__clk__o}), .bx(jogo_1_bolax), .by(jogo_1_bolay), .j1y(jogo_1_j1y),
    .j2y(jogo_1_j2y), .digito1(jogo_1_digito1), .digito10(jogo_1_digito10), .digito2(jogo_1_digito2),
    .digito20(jogo_1_digito20), .borda(pintor_1_borda), .placar2(pintor_1_placar2),
    .jogador2(pintor_1_jogador2), .placar1(pintor_1_placar1), .jogador1(pintor_1_jogador1),
    .bola(pintor_1_bola));
  and and_4 (v__de__o, vertical_mostra, horizontal_mostra);
  or or_4 (a__left__o[13], and_1_out, and_2_out, and_3_out);
  and and_5 (and_5_out, pintor_1_bola, pintor_1_jogador1);
  and and_6 (and_6_out, pintor_1_bola, pintor_1_jogador2);
  D_FF #(.Bits(15)) d_ff_2 (.D(xnor_1_out), .C(a__clk__o), .Q({d_ff_2_q[14], xnor_1_out[14:1]}));  // open: nQ
  not not_3 (not_3_out, v__de__o);
  D_FF d_ff_3 (.D(and_5_out), .C(v__clk__o), .Q(d_ff_3_q));  // open: nQ
  D_FF d_ff_4 (.D(and_6_out), .C(v__clk__o), .Q(d_ff_4_q));  // open: nQ
  xnor xnor_1 (xnor_1_out[0], xnor_1_out[14], d_ff_2_q[14]);
  PriorityEncoder #(.Selector_Bits(3)) priorityencoder_1 (
    .in0(1'b1), .in1(pintor_1_borda), .in2(pintor_1_placar2), .in3(pintor_1_jogador2),
    .in4(pintor_1_placar1), .in5(pintor_1_jogador1), .in6(pintor_1_bola), .in7(not_3_out),
    .num(priorityencoder_1_num));  // open: any
  Multiplexer #(.Selector_Bits(3), .Bits(24)) multiplexer_1 (
    .sel(priorityencoder_1_num), .in_0(24'h4000), .in_1(24'hfff0ff), .in_2(24'hff7f00), .in_3(24'hff7f00),
    .in_4(24'h7fff), .in_5(24'h7fff), .in_6(24'hffff), .in_7({24{1'b0}}), .out({v__b__o, v__g__o, v__r__o}));

  assign {a__left__o[15:14], a__left__o[12:0]} = {15{1'b0}};
  assign a__right__o = {2'b00, a__left__o[13], {13{1'b0}}};
  assign dmi__req__ready__o = 1'b0;
  assign dmi__rsp__data__o = {32{1'b0}};
  assign dmi__rsp__op__o = 2'b00;
  assign dmi__rsp__valid__o = 1'b0;
  assign led__o = {16{1'b0}};
  assign seg_o = {64{1'b0}};
  assign v__y__o[0] = a__clk__o;
  assign wb__adr__o = {32{1'b0}};
  assign wb__cyc__o = 1'b0;
  assign wb__dat__o = {32{1'b0}};
  assign wb__sel__o = 4'b0000;
  assign wb__stb__o = 1'b0;
  assign wb__we__o = 1'b0;

  // Other names for the same wires on the sheet: clk25MHz = v__clk__o

  // Notes on the sheet:
  //   640x480 60Hz, 25.175MHz, 640, 16, 96, 48, 480, 11, 2, 31
endmodule
