// Digital circuit pintor.dig as structural Verilog
// Este bloco transforma o estado do jogo numa imagem visivel na tela usando
// a informacao das coordenadas x e y do ponto que esta sendo desenhado na
// tela neste instante.
module pintor (
  input  [11:0] x,
  input  [11:0] y,
  input  [11:0] bx,
  input  [11:0] by,
  input  [11:0] j1y,
  input  [11:0] j2y,
  input  [3:0] digito1,
  input  [3:0] digito10,
  input  [3:0] digito2,
  input  [3:0] digito20,
  output borda,
  output placar2,
  output jogador2,
  output placar1,
  output jogador1,
  output bola
);

  wire and_1_out, comparator_1_lt, comparator_2_gt, comparator_3_lt, comparator_4_gt, comparator_5_lt,
       comparator_6_gt, digito_1_caracter, digito_2_caracter, digito_3_caracter, digito_4_caracter, or_3_out,
       or_4_out, retangulo_1_r;
  wire [11:0] add_1_s, add_2_s, sub_1_s, sub_2_s;

  digito digito_1 (.x(x), .y(y), .digito(digito1), .pos(5'b00110), .caracter(digito_1_caracter));
  digito digito_2 (.x(x), .y(y), .digito(digito10), .pos(5'b00101), .caracter(digito_2_caracter));
  digito digito_3 (.x(x), .y(y), .digito(digito2), .pos(5'b01111), .caracter(digito_3_caracter));
  digito digito_4 (.x(x), .y(y), .digito(digito20), .pos(5'b01110), .caracter(digito_4_caracter));
  Sub #(.Bits(12)) sub_1 (.a(bx), .b(12'h6), .c_i(1'b0), .s(sub_1_s));  // open: c_o
  Sub #(.Bits(12)) sub_2 (.a(by), .b(12'h6), .c_i(1'b0), .s(sub_2_s));  // open: c_o
  or or_1 (placar1, digito_1_caracter, digito_2_caracter);
  or or_2 (placar2, digito_3_caracter, digito_4_caracter);
  Add #(.Bits(12)) add_1 (.a(bx), .b(12'h6), .c_i(1'b0), .s(add_1_s));  // open: c_o
  Add #(.Bits(12)) add_2 (.a(by), .b(12'h6), .c_i(1'b0), .s(add_2_s));  // open: c_o
  \time  time_1 (
    .x(x), .y(y), .jy(j2y), .goleiromin(12'h255), .goleiromax(12'h260), .defesamin(12'h1e9),
    .defesamax(12'h1f7), .ataquemin(12'h101), .ataquemax(12'h10f), .jogador(jogador2));
  retangulo retangulo_1 (.x(x), .y(y), .xmin(12'h13c), .xmax(12'h144), .ymin(12'h1), .ymax(12'h1de), .r(retangulo_1_r));
  retangulo retangulo_2 (.x(x), .y(y), .xmin(sub_1_s), .xmax(add_1_s), .ymin(sub_2_s), .ymax(add_2_s), .r(bola));
  Comparator #(.Bits(12)) comparator_1 (.a(y), .b(12'h8), .lt(comparator_1_lt));  // open: gt, eq
  Comparator #(.Bits(12)) comparator_2 (.a(y), .b(12'h1d8), .gt(comparator_2_gt));  // open: eq, lt
  Comparator #(.Bits(12)) comparator_3 (.a(y), .b(12'ha0), .lt(comparator_3_lt));  // open: gt, eq
  Comparator #(.Bits(12)) comparator_4 (.a(y), .b(12'h140), .gt(comparator_4_gt));  // open: eq, lt
  Comparator #(.Bits(12)) comparator_5 (.a(x), .b(12'h18), .lt(comparator_5_lt));  // open: gt, eq
  Comparator #(.Bits(12)) comparator_6 (.a(x), .b(12'h268), .gt(comparator_6_gt));  // open: eq, lt
  \time  time_2 (
    .x(x), .y(y), .jy(j1y), .goleiromin(12'h20), .goleiromax(12'h2e), .defesamin(12'h89), .defesamax(12'h97),
    .ataquemin(12'h171), .ataquemax(12'h17f), .jogador(jogador1));
  or or_3 (or_3_out, comparator_3_lt, comparator_4_gt);
  or or_4 (or_4_out, comparator_5_lt, comparator_6_gt);
  or or_5 (borda, comparator_1_lt, retangulo_1_r, comparator_2_gt, and_1_out);
  and and_1 (and_1_out, or_3_out, or_4_out);
endmodule
