// Digital circuit retangulo.dig as structural Verilog
module retangulo (
  input  [11:0] x,
  input  [11:0] y,
  input  [11:0] xmin,
  input  [11:0] xmax,
  input  [11:0] ymin,
  input  [11:0] ymax,
  output r
);

  wire comparator_1_lt, comparator_2_gt, comparator_3_lt, comparator_4_gt;

  Comparator #(.Bits(12)) comparator_1 (.a(x), .b(xmin), .lt(comparator_1_lt));  // open: gt, eq
  Comparator #(.Bits(12)) comparator_2 (.a(x), .b(xmax), .gt(comparator_2_gt));  // open: eq, lt
  Comparator #(.Bits(12)) comparator_3 (.a(y), .b(ymin), .lt(comparator_3_lt));  // open: gt, eq
  Comparator #(.Bits(12)) comparator_4 (.a(y), .b(ymax), .gt(comparator_4_gt));  // open: eq, lt
  nor nor_1 (r, comparator_1_lt, comparator_2_gt, comparator_3_lt, comparator_4_gt);

  // Notes on the sheet:
  //   x: posicao horizontal do feixe
  //   y: posicao vertical do feixe
  //   xmin: lado esquerdo
  //   xmax: lado direito
  //   ymin: lado de cima
  //   ymax: lado de baixo
  //   r: é 1 quando o feixe está dentro do retangulo indicado
endmodule
