// Digital circuit time.dig as structural Verilog
// Um time de cinco jogadores: um goleiro, dois de defesa e dois de ataque
module \time  (
  input  [11:0] x,
  input  [11:0] y,
  input  [11:0] jy,
  input  [11:0] goleiromin,
  input  [11:0] goleiromax,
  input  [11:0] defesamin,
  input  [11:0] defesamax,
  input  [11:0] ataquemin,
  input  [11:0] ataquemax,
  output jogador
);

  wire retangulo_1_r, retangulo_2_r, retangulo_3_r, retangulo_4_r, retangulo_5_r;
  wire [11:0] add_1_s, add_2_s, add_3_s, add_4_s, add_5_s, sub_1_s, sub_2_s, sub_3_s, sub_4_s, sub_5_s;

  Sub #(.Bits(12)) sub_1 (.a(jy), .b(12'h1e), .c_i(1'b0), .s(sub_1_s));  // open: c_o
  Add #(.Bits(12)) add_1 (.a(jy), .b(12'h1e), .c_i(1'b0), .s(add_1_s));  // open: c_o
  Sub #(.Bits(12)) sub_2 (.a(jy), .b(12'h96), .c_i(1'b0), .s(sub_2_s));  // open: c_o
  Add #(.Bits(12)) add_2 (.a(jy), .b(12'h5a), .c_i(1'b0), .s(add_2_s));  // open: c_o
  retangulo retangulo_1 (
    .x(x), .y(y), .xmin(goleiromin), .xmax(goleiromax), .ymin(sub_1_s), .ymax(add_1_s), .r(retangulo_1_r));
  Sub #(.Bits(12)) sub_3 (.a(jy), .b(12'h5a), .c_i(1'b0), .s(sub_3_s));  // open: c_o
  Add #(.Bits(12)) add_3 (.a(jy), .b(12'h96), .c_i(1'b0), .s(add_3_s));  // open: c_o
  retangulo retangulo_2 (
    .x(x), .y(y), .xmin(defesamin), .xmax(defesamax), .ymin(sub_2_s), .ymax(sub_3_s), .r(retangulo_2_r));
  retangulo retangulo_3 (
    .x(x), .y(y), .xmin(defesamin), .xmax(defesamax), .ymin(add_2_s), .ymax(add_3_s), .r(retangulo_3_r));
  Sub #(.Bits(12)) sub_4 (.a(jy), .b(12'h96), .c_i(1'b0), .s(sub_4_s));  // open: c_o
  Add #(.Bits(12)) add_4 (.a(jy), .b(12'h5a), .c_i(1'b0), .s(add_4_s));  // open: c_o
  Sub #(.Bits(12)) sub_5 (.a(jy), .b(12'h5a), .c_i(1'b0), .s(sub_5_s));  // open: c_o
  Add #(.Bits(12)) add_5 (.a(jy), .b(12'h96), .c_i(1'b0), .s(add_5_s));  // open: c_o
  retangulo retangulo_4 (
    .x(x), .y(y), .xmin(ataquemin), .xmax(ataquemax), .ymin(sub_4_s), .ymax(sub_5_s), .r(retangulo_4_r));
  retangulo retangulo_5 (
    .x(x), .y(y), .xmin(ataquemin), .xmax(ataquemax), .ymin(add_4_s), .ymax(add_5_s), .r(retangulo_5_r));
  or or_1 (jogador, retangulo_4_r, retangulo_2_r, retangulo_1_r, retangulo_3_r, retangulo_5_r);
endmodule
