// Digital circuit testeCoresVGA.dig as structural Verilog
module testeCoresVGA (
  input  clk
);

  wire and_1_out, not_1_out, not_2_out, reset_1_out, temporiza_1_mostra, temporiza_1_sinc, temporiza_2_fim,
       temporiza_2_mostra, temporiza_2_sinc;
  wire [23:0] multiplexer_1_out, temporiza_1_contagem;

  Reset #(.invertOutput("false")) reset_1 (.out(reset_1_out));
  temporiza temporiza_1 (
    .relogio(clk), .conta(temporiza_2_fim), .inicializa(reset_1_out), .upix(12'h1df), .inisinc(12'h1e9),
    .fimsinc(12'h1eb), .fimcont(12'h20c), .contagem(temporiza_1_contagem[11:0]), .mostra(temporiza_1_mostra),
    .sinc(temporiza_1_sinc));  // open: fim
  temporiza temporiza_2 (
    .relogio(clk), .conta(1'b1), .inicializa(reset_1_out), .upix(12'h27f), .inisinc(12'h28f),
    .fimsinc(12'h2ef), .fimcont(12'h31f), .contagem(temporiza_1_contagem[23:12]), .fim(temporiza_2_fim),
    .mostra(temporiza_2_mostra), .sinc(temporiza_2_sinc));
  not not_1 (not_1_out, temporiza_1_sinc);
  not not_2 (not_2_out, temporiza_2_sinc);
  and and_1 (and_1_out, temporiza_1_mostra, temporiza_2_mostra);
  Multiplexer #(.Bits(24)) multiplexer_1 (
    .sel(and_1_out), .in_0({24{1'b0}}), .in_1(temporiza_1_contagem), .out(multiplexer_1_out));
  VGA vga_1 (
    .R(multiplexer_1_out[7:0]), .G(multiplexer_1_out[15:8]), .B(multiplexer_1_out[23:16]), .H(not_2_out),
    .V(not_1_out), .C(clk));

  // Notes on the sheet:
  //   clk: Hz: 2147483647
  //   640x480 60Hz, 25.175MHz, 640, 16, 96, 48, 480, 11, 2, 31
endmodule
