// Digital circuit testeQuadradosVGA.dig as structural Verilog
module testeQuadradosVGA (
  input  clk
);

  wire and_1_out, and_2_out, and_3_out, and_4_out, and_5_out, not_1_out, not_2_out, reset_1_out,
       temporiza_1_mostra, temporiza_1_sinc, temporiza_2_fim, temporiza_2_mostra, temporiza_2_sinc;
  wire [11:0] temporiza_1_contagem, temporiza_2_contagem;
  wire [23:0] multiplexer_1_out;
  wire [23:23] or_1_out;

  Reset #(.invertOutput("false")) reset_1 (.out(reset_1_out));
  temporiza temporiza_1 (
    .relogio(clk), .conta(temporiza_2_fim), .inicializa(reset_1_out), .upix(12'h1df), .inisinc(12'h1e9),
    .fimsinc(12'h1eb), .fimcont(12'h20c), .contagem(temporiza_1_contagem), .mostra(temporiza_1_mostra),
    .sinc(temporiza_1_sinc));  // open: fim
  temporiza temporiza_2 (
    .relogio(clk), .conta(1'b1), .inicializa(reset_1_out), .upix(12'h27f), .inisinc(12'h28f),
    .fimsinc(12'h2ef), .fimcont(12'h31f), .contagem(temporiza_2_contagem), .fim(temporiza_2_fim),
    .mostra(temporiza_2_mostra), .sinc(temporiza_2_sinc));
  not not_1 (not_1_out, temporiza_1_sinc);
  not not_2 (not_2_out, temporiza_2_sinc);
  and and_1 (and_1_out, temporiza_1_mostra, temporiza_2_mostra);
  Multiplexer #(.Bits(24)) multiplexer_1 (
    .sel(and_1_out), .in_0({24{1'b0}}), .in_1({24{or_1_out[23]}}), .out(multiplexer_1_out));
  VGA vga_1 (
    .R(multiplexer_1_out[7:0]), .G(multiplexer_1_out[15:8]), .B(multiplexer_1_out[23:16]), .H(not_2_out),
    .V(not_1_out), .C(clk));
  and and_2 (and_2_out, temporiza_1_contagem[1], temporiza_1_contagem[0], temporiza_1_contagem[2], temporiza_1_contagem[3]);
  and and_3 (and_3_out, ~temporiza_1_contagem[0], ~temporiza_1_contagem[1], ~temporiza_1_contagem[2], ~temporiza_1_contagem[3]);  // And
  and and_4 (and_4_out, temporiza_2_contagem[1], temporiza_2_contagem[0], temporiza_2_contagem[3], temporiza_2_contagem[2]);
  and and_5 (and_5_out, ~temporiza_2_contagem[0], ~temporiza_2_contagem[1], ~temporiza_2_contagem[2], ~temporiza_2_contagem[3]);  // And
  or or_1 (or_1_out[23], and_2_out, and_3_out, and_4_out, and_5_out);

  // Notes on the sheet:
  //   clk: Hz: 2147483647
  //   640x480 60Hz, 25.175MHz, 640, 16, 96, 48, 480, 11, 2, 31
endmodule
