// Digital circuit testeRetangulosVGA.dig as structural Verilog
module testeRetangulosVGA (
  input  clk
);

  wire and_1_out, not_1_out, not_2_out, not_3_out, reset_1_out, retangulo_1_r, retangulo_2_r,
       temporiza_1_mostra, temporiza_1_sinc, temporiza_2_fim, temporiza_2_mostra, temporiza_2_sinc;
  wire [1:0] priorityencoder_1_num;
  wire [11:0] temporiza_1_contagem, temporiza_2_contagem;
  wire [23:0] multiplexer_1_out;

  Reset #(.invertOutput("false")) reset_1 (.out(reset_1_out));
  temporiza temporiza_1 (
    .relogio(clk), .conta(temporiza_2_fim), .inicializa(reset_1_out), .upix(12'h1df), .inisinc(12'h1e9),
    .fimsinc(12'h1eb), .fimcont(12'h20c), .contagem(temporiza_1_contagem), .mostra(temporiza_1_mostra),
    .sinc(temporiza_1_sinc));  // open: fim
  temporiza temporiza_2 (
    .relogio(clk), .conta(1'b1), .inicializa(reset_1_out), .upix(12'h27f), .inisinc(12'h28f),
    .fimsinc(12'h2ef), .fimcont(12'h31f), .contagem(temporiza_2_contagem), .fim(temporiza_2_fim),
    .mostra(temporiza_2_mostra), .sinc(temporiza_2_sinc));
  not not_1 (not_1_out, temporiza_1_sinc);
  not not_2 (not_2_out, temporiza_2_sinc);
  and and_1 (and_1_out, temporiza_1_mostra, temporiza_2_mostra);
  VGA vga_1 (
    .R(multiplexer_1_out[7:0]), .G(multiplexer_1_out[15:8]), .B(multiplexer_1_out[23:16]), .H(not_2_out),
    .V(not_1_out), .C(clk));
  not not_3 (not_3_out, and_1_out);
  retangulo retangulo_1 (
    .x(temporiza_2_contagem), .y(temporiza_1_contagem), .xmin(12'h64), .xmax(12'h12c), .ymin(12'h64),
    .ymax(12'h12c), .r(retangulo_1_r));
  retangulo retangulo_2 (
    .x(temporiza_2_contagem), .y(temporiza_1_contagem), .xmin(12'hc8), .xmax(12'h1f4), .ymin(12'h96),
    .ymax(12'h190), .r(retangulo_2_r));
  PriorityEncoder #(.Selector_Bits(2)) priorityencoder_1 (
    .in0(1'b1), .in1(retangulo_1_r), .in2(retangulo_2_r), .in3(not_3_out), .num(priorityencoder_1_num));  // open: any
  Multiplexer #(.Bits(24), .Selector_Bits(2)) multiplexer_1 (
    .sel(priorityencoder_1_num), .in_0(24'h1f7f1f), .in_1(24'hffff), .in_2(24'hff), .in_3({24{1'b0}}),
    .out(multiplexer_1_out));

  // Notes on the sheet:
  //   clk: Hz: 2147483647
  //   640x480 60Hz, 25.175MHz, 640, 16, 96, 48, 480, 11, 2, 31
endmodule
