// Digital circuit testeTemporiza.dig as structural Verilog
module testeTemporiza (
  input  clk,
  output [11:0] X,
  output fim,
  output DE,
  output HS,
  output clk_2
);

  wire reset_1_out;

  Reset #(.invertOutput("false")) reset_1 (.out(reset_1_out));
  temporiza temporiza_1 (
    .relogio(clk), .conta(1'b1), .inicializa(reset_1_out), .upix(12'h7), .inisinc(12'h9), .fimsinc(12'hb),
    .fimcont(12'hd), .contagem(X), .fim(fim), .mostra(DE), .sinc(HS));

  assign clk_2 = clk;
endmodule
