// Digital circuit testeTextoVGA.dig as structural Verilog
module testeTextoVGA (
  input  clk
);

  wire and_1_out, not_1_out, not_2_out, or_1_out, reset_1_out, temporiza_1_mostra, temporiza_1_sinc,
       temporiza_2_fim, temporiza_2_mostra, temporiza_2_sinc;
  wire [1:0] temporiza_1_contagem_2;
  wire [2:0] temporiza_2_contagem;
  wire [3:0] temporiza_1_contagem;
  wire [5:0] temporiza_2_contagem_2;
  wire [7:0] char_d, multiplexer_2_out;
  wire [7:1] d_ff_1_q;
  wire [11:6] temporiza_1_contagem_3;
  wire [11:9] temporiza_2_contagem_3;
  wire [23:0] multiplexer_1_out;
  wire [23:23] d_ff_1_q_2;

  Reset #(.invertOutput("false")) reset_1 (.out(reset_1_out));
  temporiza temporiza_1 (
    .relogio(clk), .conta(temporiza_2_fim), .inicializa(reset_1_out), .upix(12'h1df), .inisinc(12'h1e9),
    .fimsinc(12'h1eb), .fimcont(12'h20c),
    .contagem({temporiza_1_contagem_3, temporiza_1_contagem_2, temporiza_1_contagem}),
    .mostra(temporiza_1_mostra), .sinc(temporiza_1_sinc));  // open: fim
  temporiza temporiza_2 (
    .relogio(clk), .conta(1'b1), .inicializa(reset_1_out), .upix(12'h27f), .inisinc(12'h28f),
    .fimsinc(12'h2ef), .fimcont(12'h31f),
    .contagem({temporiza_2_contagem_3, temporiza_2_contagem_2, temporiza_2_contagem}), .fim(temporiza_2_fim),
    .mostra(temporiza_2_mostra), .sinc(temporiza_2_sinc));
  not not_1 (not_1_out, temporiza_1_sinc);
  not not_2 (not_2_out, temporiza_2_sinc);
  and and_1 (and_1_out, temporiza_1_mostra, temporiza_2_mostra);
  Multiplexer #(.Bits(24)) multiplexer_1 (
    .sel(and_1_out), .in_0({24{1'b0}}), .in_1({24{d_ff_1_q_2[23]}}), .out(multiplexer_1_out));
  VGA vga_1 (
    .R(multiplexer_1_out[7:0]), .G(multiplexer_1_out[15:8]), .B(multiplexer_1_out[23:16]), .H(not_2_out),
    .V(not_1_out), .C(clk));
  ROM #(.AddrBits(12), .Bits(8), .isProgramMemory("true")) char (
    .A({temporiza_1_contagem_2, temporiza_2_contagem_2, temporiza_1_contagem}), .sel(1'b1), .D(char_d));
  or or_1 (or_1_out, temporiza_2_contagem[0], temporiza_2_contagem[1], temporiza_2_contagem[2]);
  Multiplexer #(.Bits(8)) multiplexer_2 (
    .sel(or_1_out), .in_0(char_d), .in_1({d_ff_1_q, 1'b0}), .out(multiplexer_2_out));
  D_FF #(.Bits(8)) d_ff_1 (.D(multiplexer_2_out), .C(clk), .Q({d_ff_1_q_2[23], d_ff_1_q}));  // open: nQ

  // Other names for the same wires on the sheet: pixclock = clk

  // Notes on the sheet:
  //   clk: Hz: 2147483647
  //   640x480 60Hz, 25.175MHz, 640, 16, 96, 48, 480, 11, 2, 31
endmodule
